// Digital circuit ADDPG_1bit.dig as structural Verilog
module ADDPG_1bit (
  input  a_i,
  input  b_i,
  input  C_in,
  output P_i,
  output G_i,
  output S
);

  wire xor_1_out;

  or or_1 (P_i, a_i, b_i);
  and and_1 (G_i, a_i, b_i);
  xor xor_1 (xor_1_out, a_i, b_i);
  xor xor_2 (S, xor_1_out, C_in);
endmodule
