// Digital circuit ADD8bits_bis.dig as structural Verilog
module ADD8bits_bis (
  input  [7:0] a,
  input  [7:0] b,
  input  [7:0] cin,
  output [7:0] S,
  output [7:0] Cout
);

  wire [7:0] and_1_out, and_2_out, xor_1_out;

  assign and_1_out = a & b;  // And and_1, 8 bits wide
  assign Cout = and_2_out | and_1_out;  // Or or_1, 8 bits wide
  assign and_2_out = cin & xor_1_out;  // And and_2, 8 bits wide
  assign xor_1_out = a ^ b;  // XOr xor_1, 8 bits wide
  assign S = cin ^ xor_1_out;  // XOr xor_2, 8 bits wide
endmodule
