// Digital circuit ADDPG8bit.dig as structural Verilog
module ADDPG8bit (
  input  a_0,
  input  b_0,
  input  C_0,
  input  a_1,
  input  b_1,
  input  a_2,
  input  b_2,
  input  a_3,
  input  b_3,
  input  a_4,
  input  b_4,
  input  a_5,
  input  b_5,
  input  a_6,
  input  b_6,
  input  a_7,
  input  b_7,
  output C_out,
  output S_0,
  output S_1,
  output S_2,
  output S_3,
  output S_4,
  output S_5,
  output S_6,
  output S_7
);

  wire addpg_1bit_1_g_i, addpg_1bit_1_p_i, addpg_1bit_2_g_i, addpg_1bit_2_p_i, addpg_1bit_3_g_i,
       addpg_1bit_3_p_i, addpg_1bit_4_g_i, addpg_1bit_4_p_i, addpg_1bit_5_g_i, addpg_1bit_5_p_i,
       addpg_1bit_6_g_i, addpg_1bit_6_p_i, addpg_1bit_7_g_i, addpg_1bit_7_p_i, addpg_1bit_8_g_i,
       addpg_1bit_8_p_i, undriven, undriven_2, undriven_3, undriven_4, undriven_5, undriven_6, undriven_7;

  ADDPG_1bit addpg_1bit_1 (.a_i(a_0), .b_i(b_0), .C_in(C_0), .P_i(addpg_1bit_1_p_i), .G_i(addpg_1bit_1_g_i), .S(S_0));
  ADDPG_1bit addpg_1bit_2 (
    .a_i(a_1), .b_i(b_1), .C_in(undriven_7), .P_i(addpg_1bit_2_p_i), .G_i(addpg_1bit_2_g_i), .S(S_1));
  ADDPG_1bit addpg_1bit_3 (
    .a_i(a_2), .b_i(b_2), .C_in(undriven_6), .P_i(addpg_1bit_3_p_i), .G_i(addpg_1bit_3_g_i), .S(S_4));
  ADDPG_1bit addpg_1bit_4 (
    .a_i(a_3), .b_i(b_3), .C_in(undriven_5), .P_i(addpg_1bit_4_p_i), .G_i(addpg_1bit_4_g_i), .S(S_2));
  ADDPG_1bit addpg_1bit_5 (
    .a_i(a_4), .b_i(b_4), .C_in(undriven_4), .P_i(addpg_1bit_5_p_i), .G_i(addpg_1bit_5_g_i), .S(S_3));
  ADDPG_1bit addpg_1bit_6 (
    .a_i(a_5), .b_i(b_5), .C_in(undriven_3), .P_i(addpg_1bit_6_p_i), .G_i(addpg_1bit_6_g_i), .S(S_5));
  ADDPG_1bit addpg_1bit_7 (
    .a_i(a_6), .b_i(b_6), .C_in(undriven_2), .P_i(addpg_1bit_7_p_i), .G_i(addpg_1bit_7_g_i), .S(S_6));
  ADDPG_1bit addpg_1bit_8 (
    .a_i(a_7), .b_i(b_7), .C_in(undriven), .P_i(addpg_1bit_8_p_i), .G_i(addpg_1bit_8_g_i), .S(S_7));
  CC_8bit cc_8bit_1 ();
endmodule
