// Digital circuit Add8bit.dig as structural Verilog
module Add8bit (
  input  a0,
  input  b0,
  input  a1,
  input  b4,
  input  a2,
  input  b1,
  input  b2,
  input  a4,
  input  a3,
  input  b3,
  input  a5,
  input  b5,
  input  a7,
  input  a6,
  input  Cin,
  input  b7,
  input  b6,
  output S0,
  output S1,
  output S2,
  output S5,
  output S6,
  output S3,
  output S4,
  output S7,
  output Cout
);

  wire add1bit_1_cout, add1bit_2_cout, add1bit_3_cout, add1bit_4_cout, add1bit_5_cout, add1bit_6_cout,
       add1bit_7_cout;

  ADD1bit add1bit_1 (.a(b0), .b(a0), .Cin(Cin), .S(S0), .Cout(add1bit_1_cout));
  ADD1bit add1bit_2 (.a(b1), .b(a1), .Cin(add1bit_1_cout), .S(S1), .Cout(add1bit_2_cout));
  ADD1bit add1bit_3 (.a(b2), .b(a2), .Cin(add1bit_2_cout), .S(S2), .Cout(add1bit_3_cout));
  ADD1bit add1bit_4 (.a(b3), .b(a3), .Cin(add1bit_3_cout), .S(S3), .Cout(add1bit_4_cout));
  ADD1bit add1bit_5 (.a(b4), .b(a4), .Cin(add1bit_4_cout), .S(S4), .Cout(add1bit_5_cout));
  ADD1bit add1bit_6 (.a(b5), .b(a5), .Cin(add1bit_5_cout), .S(S5), .Cout(add1bit_6_cout));
  ADD1bit add1bit_7 (.a(b6), .b(a6), .Cin(add1bit_6_cout), .S(S6), .Cout(add1bit_7_cout));
  ADD1bit add1bit_8 (.a(b7), .b(a7), .Cin(add1bit_7_cout), .S(S7), .Cout(Cout));
endmodule
