// Digital circuit CC_8bit.dig as structural Verilog
module CC_8bit (
  input  G0,
  input  P0,
  input  G1,
  input  P1,
  input  G2,
  input  P2,
  input  G3,
  input  P3,
  input  G4,
  input  P4,
  input  G5,
  input  P5,
  input  G6,
  input  P6,
  input  G7,
  input  P7,
  input  C0,
  output Cout0,
  output Cout1,
  output Cout2,
  output Cout3,
  output Cout4,
  output Cout5,
  output Cout6,
  output Cout7
);

  wire and_1_out, and_2_out, and_3_out, and_4_out, and_5_out, and_6_out, and_7_out, and_8_out, and_9_out,
       and_10_out, and_11_out, and_12_out, and_13_out, and_14_out, and_15_out, and_16_out, and_17_out,
       and_18_out, and_19_out, and_20_out, and_21_out, and_22_out, and_23_out, and_24_out, and_25_out,
       and_26_out, and_27_out, and_28_out, and_29_out, and_30_out, and_31_out, and_32_out, and_33_out,
       and_34_out, and_35_out, and_36_out, and_37_out, or_2_out, or_4_out, or_5_out, or_7_out, or_8_out,
       or_10_out, or_11_out, or_12_out, or_14_out, or_15_out, or_16_out, or_17_out, or_18_out, or_20_out,
       or_21_out, or_22_out, or_23_out, or_24_out, or_25_out, or_27_out, or_28_out, or_29_out, or_30_out,
       or_31_out, or_32_out, or_34_out, or_35_out, or_36_out;

  and and_1 (and_1_out, P0, C0);
  or or_1 (Cout0, G0, and_1_out);
  and and_2 (and_2_out, P1, G0);
  and and_3 (and_3_out, P1, P0);
  and and_4 (and_4_out, and_3_out, C0);
  or or_2 (or_2_out, and_4_out, and_2_out);
  or or_3 (Cout1, G1, or_2_out);
  and and_5 (and_5_out, G1, P2);
  or or_4 (or_4_out, and_6_out, and_5_out);
  and and_6 (and_6_out, and_2_out, P2);
  or or_5 (or_5_out, and_7_out, or_4_out);
  or or_6 (Cout2, G2, or_5_out);
  and and_7 (and_7_out, P2, and_4_out);
  and and_8 (and_8_out, G2, P3);
  or or_7 (or_7_out, and_9_out, and_8_out);
  and and_9 (and_9_out, P3, and_5_out);
  and and_10 (and_10_out, P3, and_7_out);
  or or_8 (or_8_out, or_10_out, or_7_out);
  or or_9 (Cout3, G3, or_8_out);
  and and_11 (and_11_out, and_6_out, P3);
  or or_10 (or_10_out, and_11_out, and_10_out);
  and and_12 (and_12_out, P4, G3);
  or or_11 (or_11_out, and_14_out, and_12_out);
  and and_13 (and_13_out, P4, and_9_out);
  and and_14 (and_14_out, P4, and_8_out);
  or or_12 (or_12_out, or_14_out, or_11_out);
  or or_13 (Cout4, or_15_out, or_12_out);
  and and_15 (and_15_out, and_10_out, P4);
  or or_14 (or_14_out, and_15_out, and_13_out);
  and and_16 (and_16_out, and_11_out, P4);
  or or_15 (or_15_out, G4, and_16_out);
  and and_17 (and_17_out, P5, G4);
  or or_16 (or_16_out, and_19_out, and_17_out);
  and and_18 (and_18_out, P5, and_14_out);
  and and_19 (and_19_out, P5, and_12_out);
  or or_17 (or_17_out, or_18_out, or_16_out);
  and and_20 (and_20_out, P5, and_13_out);
  or or_18 (or_18_out, and_20_out, and_18_out);
  or or_19 (Cout5, or_21_out, or_17_out);
  and and_21 (and_21_out, P5, and_15_out);
  or or_20 (or_20_out, and_22_out, and_21_out);
  or or_21 (or_21_out, G5, or_20_out);
  and and_22 (and_22_out, P5, and_16_out);
  and and_23 (and_23_out, P6, G5);
  or or_22 (or_22_out, and_24_out, and_23_out);
  and and_24 (and_24_out, P6, and_17_out);
  or or_23 (or_23_out, or_24_out, or_22_out);
  and and_25 (and_25_out, P6, and_19_out);
  and and_26 (and_26_out, P6, and_18_out);
  or or_24 (or_24_out, and_26_out, and_25_out);
  and and_27 (and_27_out, P6, and_20_out);
  or or_25 (or_25_out, and_28_out, and_27_out);
  or or_26 (Cout6, or_27_out, or_23_out);
  and and_28 (and_28_out, P6, and_21_out);
  or or_27 (or_27_out, or_28_out, or_25_out);
  and and_29 (and_29_out, P6, and_22_out);
  or or_28 (or_28_out, G6, and_29_out);
  and and_30 (and_30_out, P7, G6);
  and and_31 (and_31_out, P7, and_23_out);
  or or_29 (or_29_out, and_31_out, and_30_out);
  and and_32 (and_32_out, P7, and_24_out);
  or or_30 (or_30_out, and_34_out, and_32_out);
  or or_31 (or_31_out, or_30_out, or_29_out);
  and and_33 (and_33_out, P7, and_26_out);
  and and_34 (and_34_out, P7, and_25_out);
  or or_32 (or_32_out, or_35_out, or_31_out);
  or or_33 (Cout7, G7, or_32_out);
  and and_35 (and_35_out, P7, and_27_out);
  or or_34 (or_34_out, and_35_out, and_33_out);
  or or_35 (or_35_out, or_36_out, or_34_out);
  and and_36 (and_36_out, P7, and_28_out);
  or or_36 (or_36_out, and_37_out, and_36_out);
  and and_37 (and_37_out, P7, and_29_out);
endmodule
