// Digital circuit SUB_1bit.dig as structural Verilog
module SUB_1bit (
  input  b,
  input  a,
  input  sub,
  output S
);

  wire xor_1_out;

  xor xor_1 (xor_1_out, b, sub);
  ADD1bit add1bit_1 (.a(a), .b(xor_1_out), .Cin(sub), .S(S));  // open: Cout
endmodule
