// Digital circuit SUB_bis.dig as structural Verilog
module SUB_bis (
  input  [7:0] a,
  input  SUB,
  input  [7:0] b,
  output [7:0] S,
  output [7:0] C_out
);

  wire [7:0] xor_1_out;

  assign xor_1_out = b ^ {8{SUB}};  // XOr xor_1, 8 bits wide
  ADD8bits_bis add8bits_bis_1 (.a(a), .b(xor_1_out), .cin({8{SUB}}), .S(S), .Cout(C_out));
endmodule
