// Digital circuit UAL.dig as structural Verilog
module UAL (
  input  [7:0] a,
  input  [7:0] b,
  input  SUB,
  input  [2:0] C,
  output [7:0] S
);

  wire [7:0] and_8bits_1_s, or_8bits_1_s, sub_1_s, xor_8bits_1_s;

  XOR_8bits xor_8bits_1 (.a(a), .b(b), .S(xor_8bits_1_s));
  AND_8bits and_8bits_1 (.a(a), .b(b), .S(and_8bits_1_s));
  OR_8bits or_8bits_1 (.a(a), .b(b), .S(or_8bits_1_s));
  SUB sub_1 (.SUB(SUB), .b(b), .a(a), .S(sub_1_s));  // open: Cout
  Multiplexer #(.Selector_Bits(3), .Bits(8)) multiplexer_1 (
    .sel(C), .in_0(xor_8bits_1_s), .in_1(and_8bits_1_s), .in_2(or_8bits_1_s), .in_3(sub_1_s),
    .in_4({8{1'b0}}), .in_5({8{1'b0}}), .in_6({8{1'b0}}), .in_7({8{1'b0}}), .out(S));
endmodule
