// Digital circuit Banc_de_reg_32b.dig as structural Verilog
module Banc_de_reg_32b (
  input  [4:0] rs1,
  input  [4:0] rs2,
  input  [31:0] Res,
  input  [4:0] Rd,
  input  Wreg,
  output [31:0] Src1,
  output [31:0] Src2
);

  wire and_1_out, and_2_out, and_3_out, and_4_out, and_5_out, and_6_out, and_7_out, and_8_out, and_9_out,
       and_10_out, and_11_out, and_12_out, and_13_out, and_14_out, and_15_out, and_16_out, and_17_out,
       and_18_out, and_19_out, and_20_out, and_21_out, and_22_out, and_23_out, and_24_out, and_25_out,
       and_26_out, and_27_out, and_28_out, and_29_out, and_30_out, and_31_out, and_32_out, decoder_1_out_0,
       decoder_1_out_1, decoder_1_out_2, decoder_1_out_3, decoder_1_out_4, decoder_1_out_5, decoder_1_out_6,
       decoder_1_out_7, decoder_1_out_8, decoder_1_out_9, decoder_1_out_10, decoder_1_out_11,
       decoder_1_out_12, decoder_1_out_13, decoder_1_out_14, decoder_1_out_15, decoder_1_out_16,
       decoder_1_out_17, decoder_1_out_18, decoder_1_out_19, decoder_1_out_20, decoder_1_out_21,
       decoder_1_out_22, decoder_1_out_23, decoder_1_out_24, decoder_1_out_25, decoder_1_out_26,
       decoder_1_out_27, decoder_1_out_28, decoder_1_out_29, decoder_1_out_30, decoder_1_out_31,
       decoder_2_out_0, decoder_2_out_1, decoder_2_out_2, decoder_2_out_3, decoder_2_out_4, decoder_2_out_5,
       decoder_2_out_6, decoder_2_out_7, decoder_2_out_8, decoder_2_out_9, decoder_2_out_10,
       decoder_2_out_11, decoder_2_out_12, decoder_2_out_13, decoder_2_out_14, decoder_2_out_15,
       decoder_2_out_16, decoder_2_out_17, decoder_2_out_18, decoder_2_out_19, decoder_2_out_20,
       decoder_2_out_21, decoder_2_out_22, decoder_2_out_23, decoder_2_out_24, decoder_2_out_25,
       decoder_2_out_26, decoder_2_out_27, decoder_2_out_28, decoder_2_out_29, decoder_2_out_30,
       decoder_2_out_31, decoder_3_out_0, decoder_3_out_1, decoder_3_out_2, decoder_3_out_3, decoder_3_out_4,
       decoder_3_out_5, decoder_3_out_6, decoder_3_out_7, decoder_3_out_8, decoder_3_out_9, decoder_3_out_10,
       decoder_3_out_11, decoder_3_out_12, decoder_3_out_13, decoder_3_out_14, decoder_3_out_15,
       decoder_3_out_16, decoder_3_out_17, decoder_3_out_18, decoder_3_out_19, decoder_3_out_20,
       decoder_3_out_21, decoder_3_out_22, decoder_3_out_23, decoder_3_out_24, decoder_3_out_25,
       decoder_3_out_26, decoder_3_out_27, decoder_3_out_28, decoder_3_out_29, decoder_3_out_30,
       decoder_3_out_31;
  wire [31:0] X_0_q, X_1_q, X_2_q, X_3_q, X_4_q, X_5_q, X_6_q, X_7_q, X_8_q, X_9_q, X_10_q, X_11_q, X_12_q,
       X_13_q, X_14_q, X_15_q, X_16_q, X_17_q, X_18_q, X_19_q, X_20_q, X_21_q, X_22_q, X_23_q, X_24_q,
       X_25_q, X_26_q, X_27_q, X_28_q, X_29_q, X_30_q, X_31_q;

  Decoder #(.Selector_Bits(5)) decoder_1 (
    .sel(Rd), .out_0(decoder_1_out_0), .out_1(decoder_1_out_1), .out_2(decoder_1_out_2),
    .out_3(decoder_1_out_3), .out_4(decoder_1_out_4), .out_5(decoder_1_out_5), .out_6(decoder_1_out_6),
    .out_7(decoder_1_out_7), .out_8(decoder_1_out_8), .out_9(decoder_1_out_9), .out_10(decoder_1_out_10),
    .out_11(decoder_1_out_11), .out_12(decoder_1_out_12), .out_13(decoder_1_out_13),
    .out_14(decoder_1_out_14), .out_15(decoder_1_out_15), .out_16(decoder_1_out_16),
    .out_17(decoder_1_out_17), .out_18(decoder_1_out_18), .out_19(decoder_1_out_19),
    .out_20(decoder_1_out_20), .out_21(decoder_1_out_21), .out_22(decoder_1_out_22),
    .out_23(decoder_1_out_23), .out_24(decoder_1_out_24), .out_25(decoder_1_out_25),
    .out_26(decoder_1_out_26), .out_27(decoder_1_out_27), .out_28(decoder_1_out_28),
    .out_29(decoder_1_out_29), .out_30(decoder_1_out_30), .out_31(decoder_1_out_31));
  and and_1 (and_1_out, decoder_1_out_31, Wreg);
  and and_2 (and_2_out, decoder_1_out_30, Wreg);
  and and_3 (and_3_out, decoder_1_out_29, Wreg);
  and and_4 (and_4_out, decoder_1_out_28, Wreg);
  and and_5 (and_5_out, decoder_1_out_27, Wreg);
  and and_6 (and_6_out, decoder_1_out_26, Wreg);
  and and_7 (and_7_out, decoder_1_out_25, Wreg);
  and and_8 (and_8_out, decoder_1_out_24, Wreg);
  and and_9 (and_9_out, decoder_1_out_23, Wreg);
  and and_10 (and_10_out, decoder_1_out_22, Wreg);
  and and_11 (and_11_out, decoder_1_out_21, Wreg);
  and and_12 (and_12_out, decoder_1_out_20, Wreg);
  and and_13 (and_13_out, decoder_1_out_19, Wreg);
  and and_14 (and_14_out, decoder_1_out_18, Wreg);
  and and_15 (and_15_out, decoder_1_out_17, Wreg);
  and and_16 (and_16_out, decoder_1_out_16, Wreg);
  and and_17 (and_17_out, decoder_1_out_15, Wreg);
  and and_18 (and_18_out, decoder_1_out_14, Wreg);
  and and_19 (and_19_out, decoder_1_out_13, Wreg);
  and and_20 (and_20_out, decoder_1_out_12, Wreg);
  and and_21 (and_21_out, decoder_1_out_11, Wreg);
  and and_22 (and_22_out, decoder_1_out_10, Wreg);
  and and_23 (and_23_out, decoder_1_out_9, Wreg);
  and and_24 (and_24_out, decoder_1_out_8, Wreg);
  and and_25 (and_25_out, decoder_1_out_7, Wreg);
  and and_26 (and_26_out, decoder_1_out_6, Wreg);
  and and_27 (and_27_out, decoder_1_out_5, Wreg);
  and and_28 (and_28_out, decoder_1_out_4, Wreg);
  and and_29 (and_29_out, decoder_1_out_3, Wreg);
  and and_30 (and_30_out, decoder_1_out_2, Wreg);
  and and_31 (and_31_out, decoder_1_out_1, Wreg);
  and and_32 (and_32_out, decoder_1_out_0, Wreg);
  D_FF #(.Bits(32)) X_31 (.D(Res), .C(and_1_out), .Q(X_31_q));  // open: nQ
  D_FF #(.Bits(32)) X_30 (.D(Res), .C(and_2_out), .Q(X_30_q));  // open: nQ
  D_FF #(.Bits(32)) X_29 (.D(Res), .C(and_3_out), .Q(X_29_q));  // open: nQ
  D_FF #(.Bits(32)) X_28 (.D(Res), .C(and_4_out), .Q(X_28_q));  // open: nQ
  D_FF #(.Bits(32)) X_27 (.D(Res), .C(and_5_out), .Q(X_27_q));  // open: nQ
  D_FF #(.Bits(32)) X_26 (.D(Res), .C(and_6_out), .Q(X_26_q));  // open: nQ
  D_FF #(.Bits(32)) X_25 (.D(Res), .C(and_7_out), .Q(X_25_q));  // open: nQ
  D_FF #(.Bits(32)) X_24 (.D(Res), .C(and_8_out), .Q(X_24_q));  // open: nQ
  D_FF #(.Bits(32)) X_23 (.D(Res), .C(and_9_out), .Q(X_23_q));  // open: nQ
  D_FF #(.Bits(32)) X_22 (.D(Res), .C(and_10_out), .Q(X_22_q));  // open: nQ
  D_FF #(.Bits(32)) X_21 (.D(Res), .C(and_11_out), .Q(X_21_q));  // open: nQ
  D_FF #(.Bits(32)) X_20 (.D(Res), .C(and_12_out), .Q(X_20_q));  // open: nQ
  D_FF #(.Bits(32)) X_19 (.D(Res), .C(and_13_out), .Q(X_19_q));  // open: nQ
  D_FF #(.Bits(32)) X_18 (.D(Res), .C(and_14_out), .Q(X_18_q));  // open: nQ
  D_FF #(.Bits(32)) X_17 (.D(Res), .C(and_15_out), .Q(X_17_q));  // open: nQ
  D_FF #(.Bits(32)) X_16 (.D(Res), .C(and_16_out), .Q(X_16_q));  // open: nQ
  D_FF #(.Bits(32)) X_15 (.D(Res), .C(and_17_out), .Q(X_15_q));  // open: nQ
  D_FF #(.Bits(32)) X_14 (.D(Res), .C(and_18_out), .Q(X_14_q));  // open: nQ
  D_FF #(.Bits(32)) X_13 (.D(Res), .C(and_19_out), .Q(X_13_q));  // open: nQ
  D_FF #(.Bits(32)) X_12 (.D(Res), .C(and_20_out), .Q(X_12_q));  // open: nQ
  D_FF #(.Bits(32)) X_11 (.D(Res), .C(and_21_out), .Q(X_11_q));  // open: nQ
  D_FF #(.Bits(32)) X_10 (.D(Res), .C(and_22_out), .Q(X_10_q));  // open: nQ
  D_FF #(.Bits(32)) X_9 (.D(Res), .C(and_23_out), .Q(X_9_q));  // open: nQ
  D_FF #(.Bits(32)) X_8 (.D(Res), .C(and_24_out), .Q(X_8_q));  // open: nQ
  D_FF #(.Bits(32)) X_7 (.D(Res), .C(and_25_out), .Q(X_7_q));  // open: nQ
  D_FF #(.Bits(32)) X_6 (.D(Res), .C(and_26_out), .Q(X_6_q));  // open: nQ
  D_FF #(.Bits(32)) X_5 (.D(Res), .C(and_27_out), .Q(X_5_q));  // open: nQ
  D_FF #(.Bits(32)) X_4 (.D(Res), .C(and_28_out), .Q(X_4_q));  // open: nQ
  D_FF #(.Bits(32)) X_3 (.D(Res), .C(and_29_out), .Q(X_3_q));  // open: nQ
  D_FF #(.Bits(32)) X_2 (.D(Res), .C(and_30_out), .Q(X_2_q));  // open: nQ
  D_FF #(.Bits(32)) X_1 (.D(Res), .C(and_31_out), .Q(X_1_q));  // open: nQ
  D_FF #(.Bits(32)) X_0 (.D({32{1'b0}}), .C(and_32_out), .Q(X_0_q));  // open: nQ
  assign Src1 = decoder_2_out_0 ? X_0_q : 32'bz;  // Driver driver_1
  assign Src1 = decoder_2_out_2 ? X_2_q : 32'bz;  // Driver driver_2
  assign Src1 = decoder_2_out_1 ? X_1_q : 32'bz;  // Driver driver_3
  Decoder #(.Selector_Bits(5)) decoder_2 (
    .sel(rs1), .out_0(decoder_2_out_0), .out_1(decoder_2_out_1), .out_2(decoder_2_out_2),
    .out_3(decoder_2_out_3), .out_4(decoder_2_out_4), .out_5(decoder_2_out_5), .out_6(decoder_2_out_6),
    .out_7(decoder_2_out_7), .out_8(decoder_2_out_8), .out_9(decoder_2_out_9), .out_10(decoder_2_out_10),
    .out_11(decoder_2_out_11), .out_12(decoder_2_out_12), .out_13(decoder_2_out_13),
    .out_14(decoder_2_out_14), .out_15(decoder_2_out_15), .out_16(decoder_2_out_16),
    .out_17(decoder_2_out_17), .out_18(decoder_2_out_18), .out_19(decoder_2_out_19),
    .out_20(decoder_2_out_20), .out_21(decoder_2_out_21), .out_22(decoder_2_out_22),
    .out_23(decoder_2_out_23), .out_24(decoder_2_out_24), .out_25(decoder_2_out_25),
    .out_26(decoder_2_out_26), .out_27(decoder_2_out_27), .out_28(decoder_2_out_28),
    .out_29(decoder_2_out_29), .out_30(decoder_2_out_30), .out_31(decoder_2_out_31));
  assign Src1 = decoder_2_out_4 ? X_4_q : 32'bz;  // Driver driver_4
  assign Src1 = decoder_2_out_3 ? X_3_q : 32'bz;  // Driver driver_5
  assign Src1 = decoder_2_out_5 ? X_5_q : 32'bz;  // Driver driver_6
  assign Src1 = decoder_2_out_7 ? X_7_q : 32'bz;  // Driver driver_7
  assign Src1 = decoder_2_out_6 ? X_6_q : 32'bz;  // Driver driver_8
  assign Src1 = decoder_2_out_9 ? X_9_q : 32'bz;  // Driver driver_9
  assign Src1 = decoder_2_out_8 ? X_8_q : 32'bz;  // Driver driver_10
  assign Src1 = decoder_2_out_11 ? X_11_q : 32'bz;  // Driver driver_11
  assign Src1 = decoder_2_out_10 ? X_10_q : 32'bz;  // Driver driver_12
  assign Src1 = decoder_2_out_13 ? X_13_q : 32'bz;  // Driver driver_13
  assign Src1 = decoder_2_out_12 ? X_12_q : 32'bz;  // Driver driver_14
  assign Src1 = decoder_2_out_15 ? X_15_q : 32'bz;  // Driver driver_15
  assign Src1 = decoder_2_out_14 ? X_14_q : 32'bz;  // Driver driver_16
  assign Src1 = decoder_2_out_17 ? X_17_q : 32'bz;  // Driver driver_17
  assign Src1 = decoder_2_out_16 ? X_16_q : 32'bz;  // Driver driver_18
  assign Src1 = decoder_2_out_19 ? X_19_q : 32'bz;  // Driver driver_19
  assign Src1 = decoder_2_out_18 ? X_18_q : 32'bz;  // Driver driver_20
  assign Src1 = decoder_2_out_21 ? X_21_q : 32'bz;  // Driver driver_21
  assign Src1 = decoder_2_out_20 ? X_20_q : 32'bz;  // Driver driver_22
  assign Src1 = decoder_2_out_23 ? X_23_q : 32'bz;  // Driver driver_23
  assign Src1 = decoder_2_out_22 ? X_22_q : 32'bz;  // Driver driver_24
  assign Src1 = decoder_2_out_25 ? X_25_q : 32'bz;  // Driver driver_25
  assign Src1 = decoder_2_out_24 ? X_24_q : 32'bz;  // Driver driver_26
  assign Src1 = decoder_2_out_27 ? X_27_q : 32'bz;  // Driver driver_27
  assign Src1 = decoder_2_out_26 ? X_26_q : 32'bz;  // Driver driver_28
  assign Src1 = decoder_2_out_29 ? X_29_q : 32'bz;  // Driver driver_29
  assign Src1 = decoder_2_out_28 ? X_28_q : 32'bz;  // Driver driver_30
  assign Src1 = decoder_2_out_31 ? X_31_q : 32'bz;  // Driver driver_31
  assign Src1 = decoder_2_out_30 ? X_30_q : 32'bz;  // Driver driver_32
  assign Src2 = decoder_3_out_1 ? X_1_q : 32'bz;  // Driver driver_33
  assign Src2 = decoder_3_out_0 ? X_0_q : 32'bz;  // Driver driver_34
  Decoder #(.Selector_Bits(5)) decoder_3 (
    .sel(rs2), .out_0(decoder_3_out_0), .out_1(decoder_3_out_1), .out_2(decoder_3_out_2),
    .out_3(decoder_3_out_3), .out_4(decoder_3_out_4), .out_5(decoder_3_out_5), .out_6(decoder_3_out_6),
    .out_7(decoder_3_out_7), .out_8(decoder_3_out_8), .out_9(decoder_3_out_9), .out_10(decoder_3_out_10),
    .out_11(decoder_3_out_11), .out_12(decoder_3_out_12), .out_13(decoder_3_out_13),
    .out_14(decoder_3_out_14), .out_15(decoder_3_out_15), .out_16(decoder_3_out_16),
    .out_17(decoder_3_out_17), .out_18(decoder_3_out_18), .out_19(decoder_3_out_19),
    .out_20(decoder_3_out_20), .out_21(decoder_3_out_21), .out_22(decoder_3_out_22),
    .out_23(decoder_3_out_23), .out_24(decoder_3_out_24), .out_25(decoder_3_out_25),
    .out_26(decoder_3_out_26), .out_27(decoder_3_out_27), .out_28(decoder_3_out_28),
    .out_29(decoder_3_out_29), .out_30(decoder_3_out_30), .out_31(decoder_3_out_31));
  assign Src2 = decoder_3_out_3 ? X_3_q : 32'bz;  // Driver driver_35
  assign Src2 = decoder_3_out_2 ? X_2_q : 32'bz;  // Driver driver_36
  assign Src2 = decoder_3_out_4 ? X_4_q : 32'bz;  // Driver driver_37
  assign Src2 = decoder_3_out_6 ? X_6_q : 32'bz;  // Driver driver_38
  assign Src2 = decoder_3_out_5 ? X_5_q : 32'bz;  // Driver driver_39
  assign Src2 = decoder_3_out_8 ? X_8_q : 32'bz;  // Driver driver_40
  assign Src2 = decoder_3_out_7 ? X_7_q : 32'bz;  // Driver driver_41
  assign Src2 = decoder_3_out_10 ? X_10_q : 32'bz;  // Driver driver_42
  assign Src2 = decoder_3_out_9 ? X_9_q : 32'bz;  // Driver driver_43
  assign Src2 = decoder_3_out_12 ? X_12_q : 32'bz;  // Driver driver_44
  assign Src2 = decoder_3_out_11 ? X_11_q : 32'bz;  // Driver driver_45
  assign Src2 = decoder_3_out_14 ? X_14_q : 32'bz;  // Driver driver_46
  assign Src2 = decoder_3_out_13 ? X_13_q : 32'bz;  // Driver driver_47
  assign Src2 = decoder_3_out_16 ? X_16_q : 32'bz;  // Driver driver_48
  assign Src2 = decoder_3_out_15 ? X_15_q : 32'bz;  // Driver driver_49
  assign Src2 = decoder_3_out_18 ? X_18_q : 32'bz;  // Driver driver_50
  assign Src2 = decoder_3_out_17 ? X_17_q : 32'bz;  // Driver driver_51
  assign Src2 = decoder_3_out_20 ? X_20_q : 32'bz;  // Driver driver_52
  assign Src2 = decoder_3_out_19 ? X_19_q : 32'bz;  // Driver driver_53
  assign Src2 = decoder_3_out_22 ? X_22_q : 32'bz;  // Driver driver_54
  assign Src2 = decoder_3_out_21 ? X_21_q : 32'bz;  // Driver driver_55
  assign Src2 = decoder_3_out_24 ? X_24_q : 32'bz;  // Driver driver_56
  assign Src2 = decoder_3_out_23 ? X_23_q : 32'bz;  // Driver driver_57
  assign Src2 = decoder_3_out_26 ? X_26_q : 32'bz;  // Driver driver_58
  assign Src2 = decoder_3_out_25 ? X_25_q : 32'bz;  // Driver driver_59
  assign Src2 = decoder_3_out_28 ? X_28_q : 32'bz;  // Driver driver_60
  assign Src2 = decoder_3_out_27 ? X_27_q : 32'bz;  // Driver driver_61
  assign Src2 = decoder_3_out_30 ? X_30_q : 32'bz;  // Driver driver_62
  assign Src2 = decoder_3_out_29 ? X_29_q : 32'bz;  // Driver driver_63
  assign Src2 = decoder_3_out_31 ? X_31_q : 32'bz;  // Driver driver_64
endmodule
