// Digital circuit Barrel_shifter8bits.dig as structural Verilog
module Barrel_shifter8bits (
  input  E_0,
  input  E_1,
  input  E_2,
  input  E_3,
  input  E_4,
  input  E_5,
  input  E_6,
  input  E_7,
  input  C_0,
  input  C_1,
  input  C_2,
  output S_0,
  output S_1,
  output S_2,
  output S_3,
  output S_4,
  output S_5,
  output S_6,
  output S_7
);

  wire _1_1_p4, _1_2_p4, _1_3_p4, _1_4_p4, _1_5_p4, _1_6_p4, _1_7_p4, _1_8_p4, _1_9_p4, _1_10_p4, _1_11_p4,
       _1_12_p4, _1_13_p4, _1_14_p4, _1_15_p4, _1_16_p4;

  // _1 _1_1: pin names not known; wires that end beside it: E_0, 1'b0, C_0, _1_1_p4
  // _1 _1_2: pin names not known; wires that end beside it: E_1, E_0, C_0, _1_2_p4
  // _1 _1_3: pin names not known; wires that end beside it: E_2, E_1, C_0, _1_3_p4
  // _1 _1_4: pin names not known; wires that end beside it: E_3, E_2, C_0, _1_4_p4
  // _1 _1_5: pin names not known; wires that end beside it: E_4, E_3, C_0, _1_5_p4
  // _1 _1_6: pin names not known; wires that end beside it: E_5, E_4, C_0, _1_6_p4
  // _1 _1_7: pin names not known; wires that end beside it: E_6, E_5, C_0, _1_7_p4
  // _1 _1_8: pin names not known; wires that end beside it: E_7, E_6, C_0, _1_8_p4
  // _1 _1_9: pin names not known; wires that end beside it: _1_1_p4, 1'b0, C_1, _1_9_p4
  // _1 _1_10: pin names not known; wires that end beside it: _1_2_p4, 1'b0, C_1, _1_10_p4
  // _1 _1_11: pin names not known; wires that end beside it: _1_3_p4, _1_1_p4, C_1, _1_11_p4
  // _1 _1_12: pin names not known; wires that end beside it: _1_4_p4, _1_2_p4, C_1, _1_12_p4
  // _1 _1_13: pin names not known; wires that end beside it: _1_5_p4, _1_3_p4, C_1, _1_13_p4
  // _1 _1_14: pin names not known; wires that end beside it: _1_6_p4, _1_4_p4, C_1, _1_14_p4
  // _1 _1_15: pin names not known; wires that end beside it: _1_7_p4, _1_5_p4, C_1, _1_15_p4
  // _1 _1_16: pin names not known; wires that end beside it: _1_8_p4, _1_6_p4, C_1, _1_16_p4
  // _1 _1_17: pin names not known; wires that end beside it: _1_9_p4, 1'b0, C_2, S_0
  // _1 _1_18: pin names not known; wires that end beside it: _1_10_p4, 1'b0, C_2, S_1
  // _1 _1_19: pin names not known; wires that end beside it: _1_11_p4, 1'b0, C_2, S_2
  // _1 _1_20: pin names not known; wires that end beside it: _1_12_p4, 1'b0, C_2, S_3
  // _1 _1_21: pin names not known; wires that end beside it: _1_13_p4, _1_9_p4, C_2, S_4
  // _1 _1_22: pin names not known; wires that end beside it: _1_14_p4, _1_10_p4, C_2, S_5
  // _1 _1_23: pin names not known; wires that end beside it: _1_15_p4, _1_11_p4, C_2, S_6
  // _1 _1_24: pin names not known; wires that end beside it: _1_16_p4, _1_12_p4, C_2, S_7
endmodule
