// Digital circuit CC_8bits.dig as structural Verilog
module CC_8bits (
  input  P_0,
  input  G_0,
  input  P_1,
  input  G_1,
  input  P_2,
  input  G_2,
  input  P_3,
  input  G_3,
  input  P_4,
  input  G_4,
  input  P_5,
  input  G_5,
  input  P_6,
  input  G_6,
  input  P_7,
  input  G_7,
  input  C_i_0,
  output C_out_0,
  output C_out_1,
  output C_out_2,
  output C_out_3,
  output C_out_4,
  output C_out_5,
  output C_out_6,
  output C_out_7
);

  wire and_1_out, and_2_out, and_3_out, and_4_out, and_5_out, and_6_out, and_7_out, and_8_out;

  and and_1 (and_1_out, P_0, C_i_0);
  or or_1 (C_out_0, G_0, and_1_out);
  and and_2 (and_2_out, P_1, C_out_0);
  or or_2 (C_out_1, G_1, and_2_out);
  and and_3 (and_3_out, P_2, C_out_1);
  or or_3 (C_out_2, G_2, and_3_out);
  and and_4 (and_4_out, P_3, C_out_2);
  or or_4 (C_out_3, G_3, and_4_out);
  and and_5 (and_5_out, P_4, C_out_3);
  or or_5 (C_out_4, G_4, and_5_out);
  and and_6 (and_6_out, P_5, C_out_4);
  or or_6 (C_out_5, G_5, and_6_out);
  and and_7 (and_7_out, P_6, C_out_5);
  or or_7 (C_out_6, G_6, and_7_out);
  and and_8 (and_8_out, P_7, C_out_6);
  or or_8 (C_out_7, G_7, and_8_out);
endmodule
