// Digital circuit Compt_decompt.dig as structural Verilog
module Compt_decompt (
  input  reset,
  input  inc,
  input  clk,
  output Q0,
  output Q1,
  output Q2
);

  wire and_1_out, mux2vers1_1_s, mux2vers1_2_s, mux2vers1_3_s, mux2vers1_4_s, mux2vers1_5_s, mux2vers1_6_s,
       not_1_out, xnor_1_out, xnor_2_out, xor_1_out, xor_2_out;

  MUX2vers1 mux2vers1_1 (.a(Q0), .b(1'b0), .c(reset), .S(mux2vers1_1_s));
  MUX2vers1 mux2vers1_2 (.a(Q1), .b(1'b0), .c(reset), .S(mux2vers1_2_s));
  MUX2vers1 mux2vers1_3 (.a(Q2), .b(1'b0), .c(reset), .S(mux2vers1_3_s));
  xnor xnor_1 (xnor_1_out, mux2vers1_1_s, inc);
  not not_1 (not_1_out, mux2vers1_1_s);
  MUX2vers1 mux2vers1_4 (.a(xor_1_out), .b(1'b0), .c(reset), .S(mux2vers1_4_s));
  xor xor_1 (xor_1_out, xnor_1_out, mux2vers1_2_s);
  MUX2vers1 mux2vers1_5 (.a(xor_2_out), .b(1'b0), .c(reset), .S(mux2vers1_5_s));
  xnor xnor_2 (xnor_2_out, mux2vers1_2_s, inc);
  MUX2vers1 mux2vers1_6 (.a(not_1_out), .b(1'b0), .c(reset), .S(mux2vers1_6_s));
  D_FF d_ff_1 (.D(mux2vers1_6_s), .C(clk), .Q(Q0));  // open: nQ
  D_FF d_ff_2 (.D(mux2vers1_4_s), .C(clk), .Q(Q1));  // open: nQ
  D_FF d_ff_3 (.D(mux2vers1_5_s), .C(clk), .Q(Q2));  // open: nQ
  and and_1 (and_1_out, xnor_2_out, xnor_1_out);
  xor xor_2 (xor_2_out, mux2vers1_3_s, and_1_out);
endmodule
