// Digital circuit Compteur_3bits.dig as structural Verilog
module Compteur_3bits (
  input  clk,
  input  reset,
  output Q0,
  output Q1,
  output Q2
);

  wire and_1_out, mux2vers1_1_s, mux2vers1_2_s, mux2vers1_3_s, mux2vers1_4_s, not_1_out, xor_1_out, xor_2_out;

  MUX2vers1 mux2vers1_1 (.a(Q0), .b(1'b0), .c(reset), .S(mux2vers1_1_s));
  MUX2vers1 mux2vers1_2 (.a(Q1), .b(1'b0), .c(reset), .S(mux2vers1_2_s));
  MUX2vers1 mux2vers1_3 (.a(Q2), .b(1'b0), .c(reset), .S(mux2vers1_3_s));
  and and_1 (and_1_out, mux2vers1_2_s, mux2vers1_1_s);
  xor xor_1 (xor_1_out, mux2vers1_1_s, mux2vers1_2_s);
  xor xor_2 (xor_2_out, and_1_out, mux2vers1_3_s);
  MUX2vers1 mux2vers1_4 (.a(not_1_out), .b(1'b0), .c(reset), .S(mux2vers1_4_s));
  not not_1 (not_1_out, mux2vers1_1_s);
  D_FF d_ff_1 (.D(mux2vers1_4_s), .C(clk), .Q(Q0));  // open: nQ
  D_FF d_ff_2 (.D(xor_1_out), .C(clk), .Q(Q1));  // open: nQ
  D_FF d_ff_3 (.D(xor_2_out), .C(clk), .Q(Q2));  // open: nQ
endmodule
