// Digital circuit Compteur_saturation.dig as structural Verilog
module Compteur_saturation (
  input  inc,
  input  clk,
  input  reset,
  output Q0,
  output Q1,
  output Q2
);

  wire and_1_out, and_2_out, and_3_out, and_4_out, and_5_out, and_6_out, and_7_out, and_8_out, and_9_out,
       and_10_out, and_11_out, and_12_out, mux2vers1_1_s, mux2vers1_2_s, mux2vers1_3_s, or_1_out, or_2_out,
       or_3_out, or_4_out, or_5_out, or_6_out, or_7_out, or_8_out, or_9_out, xor_1_out;

  or or_1 (or_1_out, Q2, Q1);
  or or_2 (or_2_out, or_1_out, inc);
  xor xor_1 (xor_1_out, Q0, Q1);
  and and_1 (and_1_out, ~Q0, or_2_out);  // And
  and and_2 (and_2_out, xor_1_out, inc);
  and and_3 (and_3_out, Q1, Q2);
  and and_4 (and_4_out, and_3_out, inc);
  and and_5 (and_5_out, ~Q0, ~Q1);  // And
  or or_3 (or_3_out, and_4_out, and_1_out);
  and and_6 (and_6_out, and_5_out, Q2);
  MUX2vers1 mux2vers1_1 (.a(or_3_out), .b(1'b0), .c(reset), .S(mux2vers1_1_s));
  D_FF d_ff_1 (.D(mux2vers1_1_s), .C(clk), .Q(Q0));  // open: nQ
  and and_7 (and_7_out, Q0, Q1);
  or or_4 (or_4_out, and_7_out, and_6_out);
  or or_5 (or_5_out, Q1, Q0);
  and and_8 (and_8_out, or_4_out, ~inc);  // And
  and and_9 (and_9_out, Q1, Q0);
  and and_10 (and_10_out, and_9_out, Q2);
  and and_11 (and_11_out, Q2, or_5_out);
  or or_6 (or_6_out, and_10_out, and_8_out);
  or or_7 (or_7_out, and_7_out, Q2);
  and and_12 (and_12_out, or_7_out, inc);
  MUX2vers1 mux2vers1_2 (.a(or_8_out), .b(1'b0), .c(reset), .S(mux2vers1_2_s));
  or or_8 (or_8_out, or_6_out, and_2_out);
  or or_9 (or_9_out, and_11_out, and_12_out);
  D_FF d_ff_2 (.D(mux2vers1_2_s), .C(clk), .Q(Q1));  // open: nQ
  MUX2vers1 mux2vers1_3 (.a(or_9_out), .b(1'b0), .c(reset), .S(mux2vers1_3_s));
  D_FF d_ff_3 (.D(mux2vers1_3_s), .C(clk), .Q(Q2));  // open: nQ
endmodule
