// Digital circuit MUX2vers1.dig as structural Verilog
module MUX2vers1 (
  input  a,
  input  b,
  input  c,
  output S
);

  wire and_1_out, and_2_out;

  and and_1 (and_1_out, a, ~c);  // And
  and and_2 (and_2_out, b, c);
  or or_1 (S, and_1_out, and_2_out);
endmodule
