// Digital circuit Datapath1.1.dig as structural Verilog
module Datapath1_1 (
  input  MUX_MDR,
  input  M_WRITE,
  input  G_MDR,
  input  G_ALU,
  input  G_PC,
  input  W_PC,
  input  W_RI,
  input  W_MAR,
  input  W_MDR,
  input  W_REG
);

  wire [31:0] ADD_s, banc_de_reg_32b_1_src1, banc_de_reg_32b_1_src2, driver_1_out, MAR_q, MDR_q, MEM_d,
       multiplexer_1_out, PC_q, RI_q, ual_32b_1_s;

  D_FF #(.Bits(32)) PC (.D(ADD_s), .C(W_PC), .Q(PC_q));  // open: nQ
  assign driver_1_out = G_PC ? PC_q : 32'bz;  // Driver driver_1
  Add #(.Bits(32)) ADD (.a(PC_q), .b(32'h4), .c_i(1'b0), .s(ADD_s));  // open: c_o
  D_FF #(.Bits(32)) RI (.D(driver_1_out), .C(W_RI), .Q(RI_q));  // open: nQ
  D_FF #(.Bits(32)) MAR (.D(driver_1_out), .C(W_MAR), .Q(MAR_q));  // open: nQ
  Banc_de_reg_32b banc_de_reg_32b_1 (
    .rs1(RI_q[19:15]), .rs2(RI_q[24:20]), .Res(driver_1_out), .Rd(RI_q[11:7]), .Wreg(W_REG),
    .Src1(banc_de_reg_32b_1_src1), .Src2(banc_de_reg_32b_1_src2));
  RAMSinglePortSel #(.AddrBits(6), .Bits(32)) MEM (.A(MAR_q[31:26]), .CS(1'b1), .WE(M_WRITE), .OE(~M_WRITE), .D(MEM_d));
  UAL_32b ual_32b_1 (
    .a(banc_de_reg_32b_1_src1), .b(banc_de_reg_32b_1_src2), .SUB(RI_q[30]), .f3(RI_q[14:12]), .S(ual_32b_1_s));
  Multiplexer #(.Bits(32)) multiplexer_1 (.sel(MUX_MDR), .in_0(MEM_d), .in_1(driver_1_out), .out(multiplexer_1_out));
  D_FF #(.Bits(32)) MDR (.D(multiplexer_1_out), .C(W_MDR), .Q(MDR_q));  // open: nQ
  assign MEM_d = M_WRITE ? MDR_q : 32'bz;  // Driver driver_2
  assign driver_1_out = G_ALU ? ual_32b_1_s : 32'bz;  // Driver driver_3
  assign driver_1_out = G_MDR ? MDR_q : 32'bz;  // Driver driver_4
endmodule
