// Digital circuit Decodeur38.dig as structural Verilog
module Decodeur3_8 (
  input  e0,
  input  e1,
  input  e2,
  output S0,
  output S1,
  output S2,
  output S3,
  output S4,
  output S5,
  output S6,
  output S7
);

  wire and_1_out, and_2_out, and_3_out, and_4_out, and_5_out, and_6_out, and_7_out, and_8_out;

  and and_1 (and_1_out, ~e0, ~e1);  // And
  and and_2 (and_2_out, e0, ~e1);  // And
  and and_3 (and_3_out, ~e0, e1);  // And
  and and_4 (and_4_out, e0, e1);
  and and_5 (and_5_out, ~e1, ~e0);  // And
  and and_6 (and_6_out, e0, ~e1);  // And
  and and_7 (and_7_out, ~e0, e1);  // And
  and and_8 (and_8_out, e0, e1);
  and and_9 (S0, ~e2, and_1_out);  // And
  and and_10 (S1, ~e2, and_2_out);  // And
  and and_11 (S2, ~e2, and_3_out);  // And
  and and_12 (S3, ~e2, and_4_out);  // And
  and and_13 (S4, e2, and_5_out);
  and and_14 (S5, e2, and_6_out);
  and and_15 (S6, e2, and_7_out);
  and and_16 (S7, e2, and_8_out);
endmodule
