// Digital circuit ADDPG_1bit.dig as structural Verilog
module ADDPG_1bit (
  input  Ai,
  input  Bi,
  input  Cin,
  output Pi,
  output Gi,
  output Si
);

  wire xor_1_out;

  or or_1 (Pi, Ai, Bi);
  and and_1 (Gi, Ai, Bi);
  xor xor_1 (xor_1_out, Ai, Bi);
  xor xor_2 (Si, xor_1_out, Cin);
endmodule
