// Digital circuit Add8bit.dig as structural Verilog
module Add8bit (
  input  I1,
  input  I2,
  input  I3,
  input  I10,
  input  I5,
  input  I4,
  input  I6,
  input  I9,
  input  I7,
  input  I8,
  input  I11,
  input  I12,
  input  I15,
  input  I13,
  input  Cin,
  input  I16,
  input  I14,
  output S1,
  output S2,
  output S3,
  output S6,
  output S7,
  output S4,
  output S5,
  output S8,
  output Cout
);

  wire add_1bit_1_cout, add_1bit_2_cout, add_1bit_3_cout, add_1bit_4_cout, add_1bit_5_cout, add_1bit_6_cout,
       add_1bit_7_cout;

  Add_1bit add_1bit_1 (.A(I2), .B(I1), .Cin(Cin), .S(S1), .Cout(add_1bit_1_cout));
  Add_1bit add_1bit_2 (.A(I4), .B(I3), .Cin(add_1bit_1_cout), .S(S2), .Cout(add_1bit_2_cout));
  Add_1bit add_1bit_3 (.A(I6), .B(I5), .Cin(add_1bit_2_cout), .S(S3), .Cout(add_1bit_3_cout));
  Add_1bit add_1bit_4 (.A(I8), .B(I7), .Cin(add_1bit_3_cout), .S(S4), .Cout(add_1bit_4_cout));
  Add_1bit add_1bit_5 (.A(I10), .B(I9), .Cin(add_1bit_4_cout), .S(S5), .Cout(add_1bit_5_cout));
  Add_1bit add_1bit_6 (.A(I12), .B(I11), .Cin(add_1bit_5_cout), .S(S6), .Cout(add_1bit_6_cout));
  Add_1bit add_1bit_7 (.A(I14), .B(I13), .Cin(add_1bit_6_cout), .S(S7), .Cout(add_1bit_7_cout));
  Add_1bit add_1bit_8 (.A(I16), .B(I15), .Cin(add_1bit_7_cout), .S(S8), .Cout(Cout));
endmodule
