// Digital circuit Calcul_ret_1bit.dig as structural Verilog
module Calcul_ret_1bit (
  input  Pi,
  input  Cini,
  input  Gi,
  output Couti
);

  wire and_1_out;

  and and_1 (and_1_out, Pi, Cini);
  or or_1 (Couti, and_1_out, Gi);
endmodule
