// Digital circuit Datapath.dig as structural Verilog
module Datapath (
  input  [31:0] WPC,
  input  [31:0] Wreg
);

  wire banc_de_32_registres_1_p3, banc_de_32_registres_1_p4;

  // banc_de_32_registres banc_de_32_registres_1: pin names not known; wires that end beside it: WPC, Wreg, banc_de_32_registres_1_p3, banc_de_32_registres_1_p4
  // UAL_Sam ual_sam_1: pin names not known; wires that end beside it: banc_de_32_registres_1_p3, banc_de_32_registres_1_p4
endmodule
