// Digital circuit Decodeur 3vers8.dig as structural Verilog
module Decodeur_3vers8 (
  input  E0,
  input  E1,
  input  E2,
  output S0,
  output S1,
  output S2,
  output S3,
  output S4,
  output S5,
  output S6,
  output S7
);

  wire not_1_out, not_2_out, not_3_out;

  not not_1 (not_1_out, E0);
  not not_2 (not_2_out, E1);
  not not_3 (not_3_out, E2);
  and and_1 (S0, not_3_out, not_2_out, not_1_out);
  and and_2 (S1, E2, not_2_out, not_1_out);
  and and_3 (S2, not_3_out, E1, not_1_out);
  and and_4 (S3, E2, E1, not_1_out);
  and and_5 (S4, not_3_out, not_2_out, E0);
  and and_6 (S5, E2, not_2_out, E0);
  and and_7 (S6, not_3_out, E1, E0);
  and and_8 (S7, E2, E1, E0);
endmodule
