// Digital circuit Exo5.dig as structural Verilog
module Exo5 (
  input  [7:0] A,
  input  [7:0] B,
  input  [7:0] A_2,
  input  [7:0] B_2,
  output [7:0] S,
  output [7:0] S_2
);

  assign S = A ^ B;  // XOr xor_1, 8 bits wide
  assign S_2 = A_2 | B_2;  // Or or_1, 8 bits wide
endmodule
