// Digital circuit MUX 2entrees.dig as structural Verilog
module MUX_2entrees (
  input  I0,
  input  I1,
  input  A,
  output S
);

  wire and_1_out, and_2_out, not_1_out;

  not not_1 (not_1_out, A);
  and and_1 (and_1_out, I0, not_1_out);
  and and_2 (and_2_out, A, I1);
  or or_1 (S, and_1_out, and_2_out);
endmodule
