// Digital circuit MUX à 8entrées.dig as structural Verilog
module \MUX_à_8entrées  (
  input  I0,
  input  I1,
  input  S0,
  input  I2,
  input  I3,
  input  I4,
  input  I5,
  input  I6,
  input  I7,
  input  S1,
  input  S2,
  output Y
);

  wire mux_2entrees_1_s, mux_2entrees_2_s, mux_2entrees_3_s, mux_2entrees_4_s, mux_2entrees_5_s,
       mux_2entrees_6_s;

  MUX_2entrees mux_2entrees_1 (.I0(I0), .I1(I1), .A(S0), .S(mux_2entrees_1_s));
  MUX_2entrees mux_2entrees_2 (.I0(I2), .I1(I3), .A(S0), .S(mux_2entrees_2_s));
  MUX_2entrees mux_2entrees_3 (.I0(I4), .I1(I5), .A(S0), .S(mux_2entrees_3_s));
  MUX_2entrees mux_2entrees_4 (.I0(I6), .I1(I7), .A(S0), .S(mux_2entrees_4_s));
  MUX_2entrees mux_2entrees_5 (.I0(mux_2entrees_1_s), .I1(mux_2entrees_2_s), .A(S1), .S(mux_2entrees_5_s));
  MUX_2entrees mux_2entrees_6 (.I0(mux_2entrees_3_s), .I1(mux_2entrees_4_s), .A(S1), .S(mux_2entrees_6_s));
  MUX_2entrees mux_2entrees_7 (.I0(mux_2entrees_5_s), .I1(mux_2entrees_6_s), .A(S2), .S(Y));
endmodule
