// Digital circuit MUX à 8entrées_non_rec.dig as structural Verilog
module \MUX_à_8entrées_non_rec  (
  input  I0,
  input  I1,
  input  S0,
  input  I2,
  input  I3,
  input  I4,
  input  I5,
  input  I6,
  input  I7,
  input  S1,
  input  S2,
  output Y
);

  wire and_1_out, and_2_out, and_3_out, and_4_out, and_5_out, and_6_out, and_7_out, and_8_out, and_9_out,
       and_10_out, and_11_out, and_12_out, and_13_out, and_14_out, not_1_out, not_2_out, not_3_out, or_1_out,
       or_2_out, or_3_out, or_4_out, or_5_out, or_6_out;

  not not_1 (not_1_out, S0);
  not not_2 (not_2_out, S1);
  not not_3 (not_3_out, S2);
  and and_1 (and_1_out, I2, not_1_out);
  and and_2 (and_2_out, I3, S0);
  and and_3 (and_3_out, I4, not_1_out);
  and and_4 (and_4_out, I5, S0);
  and and_5 (and_5_out, I6, not_1_out);
  and and_6 (and_6_out, I7, S0);
  and and_7 (and_7_out, I0, not_1_out);
  and and_8 (and_8_out, S0, I1);
  or or_1 (or_1_out, and_1_out, and_2_out);
  or or_2 (or_2_out, and_3_out, and_4_out);
  or or_3 (or_3_out, and_5_out, and_6_out);
  or or_4 (or_4_out, and_7_out, and_8_out);
  and and_9 (and_9_out, or_4_out, not_2_out);
  and and_10 (and_10_out, S1, or_1_out);
  and and_11 (and_11_out, not_2_out, or_2_out);
  and and_12 (and_12_out, S1, or_3_out);
  or or_5 (or_5_out, and_9_out, and_10_out);
  or or_6 (or_6_out, and_11_out, and_12_out);
  and and_13 (and_13_out, or_5_out, not_3_out);
  and and_14 (and_14_out, S2, or_6_out);
  or or_7 (Y, and_13_out, and_14_out);
endmodule
