// Digital circuit MUX_8en_rec.dig as structural Verilog
module MUX_8en_rec (
  input  e0,
  input  e1,
  input  e2,
  input  e3,
  input  e4,
  input  e5,
  input  e6,
  input  e7,
  input  C0,
  input  C1,
  input  C2,
  output S
);

  wire mux_2entrees_1_s, mux_2entrees_2_s, mux_2entrees_3_s, mux_2entrees_4_s, mux_2entrees_5_s,
       mux_2entrees_6_s;

  MUX_2entrees mux_2entrees_1 (.I0(e0), .I1(e1), .A(C0), .S(mux_2entrees_1_s));
  MUX_2entrees mux_2entrees_2 (.I0(e2), .I1(e3), .A(C0), .S(mux_2entrees_2_s));
  MUX_2entrees mux_2entrees_3 (.I0(e4), .I1(e5), .A(C0), .S(mux_2entrees_3_s));
  MUX_2entrees mux_2entrees_4 (.I0(e6), .I1(e7), .A(C0), .S(mux_2entrees_4_s));
  MUX_2entrees mux_2entrees_5 (.I0(mux_2entrees_1_s), .I1(mux_2entrees_2_s), .A(C1), .S(mux_2entrees_5_s));
  MUX_2entrees mux_2entrees_6 (.I0(mux_2entrees_3_s), .I1(mux_2entrees_4_s), .A(C1), .S(mux_2entrees_6_s));
  MUX_2entrees mux_2entrees_7 (.I0(mux_2entrees_5_s), .I1(mux_2entrees_6_s), .A(C2), .S(S));
endmodule
