// Digital circuit Registre_8bits.dig as structural Verilog
module Registre_8bits (
  input  D0,
  input  CLK,
  output Q0,
  output Q1,
  output Q2,
  output Q3,
  output Q4,
  output Q5,
  output Q6,
  output Q7,
  output Q_0,
  output Q_1,
  output Q_2,
  output Q_3,
  output Q_4,
  output Q_5,
  output Q_6,
  output Q_7
);

  D_FF d_ff_1 (.D(D0), .C(CLK), .Q(Q0), .nQ(Q_0));
  D_FF d_ff_2 (.D(D0), .C(CLK), .Q(Q1), .nQ(Q_1));
  D_FF d_ff_3 (.D(D0), .C(CLK), .Q(Q2), .nQ(Q_2));
  D_FF d_ff_4 (.D(D0), .C(CLK), .Q(Q3), .nQ(Q_3));
  D_FF d_ff_5 (.D(D0), .C(CLK), .Q(Q4), .nQ(Q_4));
  D_FF d_ff_6 (.D(D0), .C(CLK), .Q(Q5), .nQ(Q_5));
  D_FF d_ff_7 (.D(D0), .C(CLK), .Q(Q6), .nQ(Q_6));
  D_FF d_ff_8 (.D(D0), .C(CLK), .Q(Q7), .nQ(Q_7));
endmodule
