// Digital circuit Registre_decalage_g&d.dig as structural Verilog
module Registre_decalage_g_d (
  input  [1:0] DEC,
  input  W,
  input  E0,
  input  E1,
  input  E2,
  input  E3,
  input  E4,
  input  E5,
  input  E6,
  input  E7,
  input  left
);

  wire d_ff_1_q, d_ff_2_q, d_ff_3_q, d_ff_4_q, d_ff_5_q, d_ff_6_q, d_ff_7_q, d_ff_8_q, multiplexer_1_out,
       multiplexer_2_out, multiplexer_3_out, multiplexer_4_out, multiplexer_5_out, multiplexer_6_out,
       multiplexer_7_out, multiplexer_8_out;

  Multiplexer #(.Selector_Bits(2)) multiplexer_1 (
    .sel(DEC), .in_0(E0), .in_1(E0), .in_2(d_ff_8_q), .in_3(left), .out(multiplexer_1_out));
  D_FF d_ff_1 (.D(multiplexer_1_out), .C(W), .Q(d_ff_1_q));  // open: nQ
  Multiplexer multiplexer_2 (.sel(DEC[0]), .in_0(E1), .in_1(d_ff_1_q), .out(multiplexer_2_out));
  D_FF d_ff_2 (.D(multiplexer_2_out), .C(W), .Q(d_ff_2_q));  // open: nQ
  Multiplexer multiplexer_3 (.sel(DEC[0]), .in_0(E2), .in_1(d_ff_2_q), .out(multiplexer_3_out));
  D_FF d_ff_3 (.D(multiplexer_3_out), .C(W), .Q(d_ff_3_q));  // open: nQ
  Multiplexer multiplexer_4 (.sel(DEC[0]), .in_0(E3), .in_1(d_ff_3_q), .out(multiplexer_4_out));
  D_FF d_ff_4 (.D(multiplexer_4_out), .C(W), .Q(d_ff_4_q));  // open: nQ
  Multiplexer multiplexer_5 (.sel(DEC[0]), .in_0(E4), .in_1(d_ff_4_q), .out(multiplexer_5_out));
  D_FF d_ff_5 (.D(multiplexer_5_out), .C(W), .Q(d_ff_5_q));  // open: nQ
  Multiplexer multiplexer_6 (.sel(DEC[0]), .in_0(E5), .in_1(d_ff_5_q), .out(multiplexer_6_out));
  D_FF d_ff_6 (.D(multiplexer_6_out), .C(W), .Q(d_ff_6_q));  // open: nQ
  Multiplexer multiplexer_7 (.sel(DEC[0]), .in_0(E6), .in_1(d_ff_6_q), .out(multiplexer_7_out));
  D_FF d_ff_7 (.D(multiplexer_7_out), .C(W), .Q(d_ff_7_q));  // open: nQ
  Multiplexer multiplexer_8 (.sel(DEC[0]), .in_0(E7), .in_1(d_ff_7_q), .out(multiplexer_8_out));
  D_FF d_ff_8 (.D(multiplexer_8_out), .C(W), .Q(d_ff_8_q));  // open: nQ
  // Pins of 1 and 2 bits meet at DEC
endmodule
