// Digital circuit UAL_Sam.dig as structural Verilog
module UAL_Sam (
  input  [31:0] E0,
  input  [31:0] E1,
  input  [3:0] F3,
  input  Ci,
  output [31:0] S
);

  wire [31:0] add_1_s, add_2_s, and_1_out, nand_1_out, nor_1_out, not_1_out, not_2_out, not_3_out, or_1_out,
       xor_1_out;

  assign not_1_out = ~E1;  // Not not_1, 32 bits wide
  assign and_1_out = E0 & E1;  // And and_1, 32 bits wide
  assign nand_1_out = ~(E0 & E1);  // NAnd nand_1, 32 bits wide
  assign or_1_out = E0 | E1;  // Or or_1, 32 bits wide
  assign nor_1_out = ~(E0 | E1);  // NOr nor_1, 32 bits wide
  assign xor_1_out = E0 ^ E1;  // XOr xor_1, 32 bits wide
  Add #(.Bits(32)) add_1 (.a(E0), .b(E1), .c_i(Ci), .s(add_1_s));  // open: c_o
  Add #(.Bits(32)) add_2 (.a(E0), .b(not_1_out), .c_i(Ci), .s(add_2_s));  // open: c_o
  assign not_2_out = ~E0;  // Not not_2, 32 bits wide
  assign not_3_out = ~E1;  // Not not_3, 32 bits wide
  Multiplexer #(.Selector_Bits(4), .Bits(32)) multiplexer_1 (
    .sel(F3), .in_0(and_1_out), .in_1(nand_1_out), .in_2(or_1_out), .in_3(nor_1_out), .in_4(xor_1_out),
    .in_5(add_1_s), .in_6(add_2_s), .in_7(not_2_out), .in_8(not_3_out), .in_9({32{1'b0}}),
    .in_10({32{1'b0}}), .in_11({32{1'b0}}), .in_12({32{1'b0}}), .in_13({32{1'b0}}), .in_14({32{1'b0}}),
    .in_15({32{1'b0}}), .out(S));
endmodule
