// Digital circuit banc de 32 registres.dig as structural Verilog
module banc_de_32_registres (
  input  [31:0] RES,
  input  [4:0] RD,
  input  [4:0] RS1,
  input  [4:0] RS2,
  input  Wreg,
  output [31:0] SRC1,
  output [31:0] SRC2
);

  wire and_1_out, and_2_out, and_3_out, and_4_out, decoder_1_out_0, decoder_1_out_1, decoder_1_out_2,
       decoder_1_out_3;
  wire [31:0] banc_de_registre_avec_r0_1_src1, banc_de_registre_avec_r0_1_src2,
       banc_de_registre_sans_r0_1_src1, banc_de_registre_sans_r0_1_src2, banc_de_registre_sans_r0_2_src1,
       banc_de_registre_sans_r0_2_src2, banc_de_registre_sans_r0_3_src1, banc_de_registre_sans_r0_3_src2;

  Decoder #(.Selector_Bits(2)) decoder_1 (
    .sel(RD[4:3]), .out_0(decoder_1_out_0), .out_1(decoder_1_out_1), .out_2(decoder_1_out_2),
    .out_3(decoder_1_out_3));
  and and_1 (and_1_out, decoder_1_out_0, Wreg);
  and and_2 (and_2_out, decoder_1_out_1, Wreg);
  and and_3 (and_3_out, decoder_1_out_2, Wreg);
  and and_4 (and_4_out, decoder_1_out_3, Wreg);
  banc_de_registre_avec_r0 banc_de_registre_avec_r0_1 (
    .rd(RD[2:0]), .res(RES), .Wreg(and_1_out), .rs1(RS1[2:0]), .rs2(RS2[2:0]),
    .SRC1(banc_de_registre_avec_r0_1_src1), .SRC2(banc_de_registre_avec_r0_1_src2));
  banc_de_registre_sans_r0 banc_de_registre_sans_r0_1 (
    .rd(RD[2:0]), .res(RES), .Wreg(and_2_out), .rs1(RS1[2:0]), .rs2(RS2[2:0]),
    .SRC1(banc_de_registre_sans_r0_1_src1), .SRC2(banc_de_registre_sans_r0_1_src2));
  banc_de_registre_sans_r0 banc_de_registre_sans_r0_2 (
    .rd(RD[2:0]), .res(RES), .Wreg(and_3_out), .rs1(RS1[2:0]), .rs2(RS2[2:0]),
    .SRC1(banc_de_registre_sans_r0_2_src1), .SRC2(banc_de_registre_sans_r0_2_src2));
  banc_de_registre_sans_r0 banc_de_registre_sans_r0_3 (
    .rd(RD[2:0]), .res(RES), .Wreg(and_4_out), .rs1(RS1[2:0]), .rs2(RS2[2:0]),
    .SRC1(banc_de_registre_sans_r0_3_src1), .SRC2(banc_de_registre_sans_r0_3_src2));
  Multiplexer #(.Selector_Bits(2), .Bits(32)) multiplexer_1 (
    .sel(RS2[4:3]), .in_0(banc_de_registre_avec_r0_1_src2), .in_1(banc_de_registre_sans_r0_1_src2),
    .in_2(banc_de_registre_sans_r0_2_src2), .in_3(banc_de_registre_sans_r0_3_src2), .out(SRC2));
  Multiplexer #(.Selector_Bits(2), .Bits(32)) multiplexer_2 (
    .sel(RS1[4:3]), .in_0(banc_de_registre_avec_r0_1_src1), .in_1(banc_de_registre_sans_r0_1_src1),
    .in_2(banc_de_registre_sans_r0_2_src1), .in_3(banc_de_registre_sans_r0_3_src1), .out(SRC1));
endmodule
