// Digital circuit banc de registre avec r0.dig as structural Verilog
module banc_de_registre_avec_r0 (
  input  [2:0] rd,
  input  [31:0] res,
  input  Wreg,
  input  [2:0] rs1,
  input  [2:0] rs2,
  output [31:0] SRC1,
  output [31:0] SRC2
);

  wire and_1_out, and_2_out, and_3_out, and_4_out, and_5_out, and_6_out, and_7_out, and_8_out,
       decoder_1_out_0, decoder_1_out_1, decoder_1_out_2, decoder_1_out_3, decoder_1_out_4, decoder_1_out_5,
       decoder_1_out_6, decoder_1_out_7, decoder_2_out_0, decoder_2_out_1, decoder_2_out_2, decoder_2_out_3,
       decoder_2_out_4, decoder_2_out_5, decoder_2_out_6, decoder_2_out_7, decoder_3_out_0, decoder_3_out_1,
       decoder_3_out_2, decoder_3_out_3, decoder_3_out_4, decoder_3_out_5, decoder_3_out_6, decoder_3_out_7;
  wire [31:0] r0_q, r1_q, r2_q, r3_q, r4_q, r5_q, r6_q, r7_q;

  Decoder #(.Selector_Bits(3)) decoder_1 (
    .sel(rd), .out_0(decoder_1_out_0), .out_1(decoder_1_out_1), .out_2(decoder_1_out_2),
    .out_3(decoder_1_out_3), .out_4(decoder_1_out_4), .out_5(decoder_1_out_5), .out_6(decoder_1_out_6),
    .out_7(decoder_1_out_7));
  and and_1 (and_1_out, decoder_1_out_0, Wreg);
  and and_2 (and_2_out, decoder_1_out_1, Wreg);
  and and_3 (and_3_out, decoder_1_out_2, Wreg);
  and and_4 (and_4_out, decoder_1_out_3, Wreg);
  and and_5 (and_5_out, decoder_1_out_4, Wreg);
  and and_6 (and_6_out, decoder_1_out_5, Wreg);
  and and_7 (and_7_out, decoder_1_out_6, Wreg);
  and and_8 (and_8_out, decoder_1_out_7, Wreg);
  D_FF #(.Bits(32)) r0 (.D({32{1'b0}}), .C(and_1_out), .Q(r0_q));  // open: nQ
  D_FF #(.Bits(32)) r1 (.D(res), .C(and_2_out), .Q(r1_q));  // open: nQ
  D_FF #(.Bits(32)) r2 (.D(res), .C(and_3_out), .Q(r2_q));  // open: nQ
  D_FF #(.Bits(32)) r3 (.D(res), .C(and_4_out), .Q(r3_q));  // open: nQ
  D_FF #(.Bits(32)) r4 (.D(res), .C(and_5_out), .Q(r4_q));  // open: nQ
  D_FF #(.Bits(32)) r5 (.D(res), .C(and_6_out), .Q(r5_q));  // open: nQ
  D_FF #(.Bits(32)) r6 (.D(res), .C(and_7_out), .Q(r6_q));  // open: nQ
  D_FF #(.Bits(32)) r7 (.D(res), .C(and_8_out), .Q(r7_q));  // open: nQ
  assign SRC1 = decoder_2_out_0 ? r0_q : 32'bz;  // Driver driver_1
  assign SRC1 = decoder_2_out_1 ? r1_q : 32'bz;  // Driver driver_2
  Decoder #(.Selector_Bits(3)) decoder_2 (
    .sel(rs1), .out_0(decoder_2_out_0), .out_1(decoder_2_out_1), .out_2(decoder_2_out_2),
    .out_3(decoder_2_out_3), .out_4(decoder_2_out_4), .out_5(decoder_2_out_5), .out_6(decoder_2_out_6),
    .out_7(decoder_2_out_7));
  assign SRC1 = decoder_2_out_2 ? r2_q : 32'bz;  // Driver driver_3
  assign SRC1 = decoder_2_out_3 ? r3_q : 32'bz;  // Driver driver_4
  assign SRC1 = decoder_2_out_4 ? r4_q : 32'bz;  // Driver driver_5
  assign SRC1 = decoder_2_out_5 ? r5_q : 32'bz;  // Driver driver_6
  assign SRC1 = decoder_2_out_6 ? r6_q : 32'bz;  // Driver driver_7
  assign SRC1 = decoder_2_out_7 ? r7_q : 32'bz;  // Driver driver_8
  assign SRC2 = decoder_3_out_0 ? r0_q : 32'bz;  // Driver driver_9
  assign SRC2 = decoder_3_out_1 ? r1_q : 32'bz;  // Driver driver_10
  Decoder #(.Selector_Bits(3)) decoder_3 (
    .sel(rs2), .out_0(decoder_3_out_0), .out_1(decoder_3_out_1), .out_2(decoder_3_out_2),
    .out_3(decoder_3_out_3), .out_4(decoder_3_out_4), .out_5(decoder_3_out_5), .out_6(decoder_3_out_6),
    .out_7(decoder_3_out_7));
  assign SRC2 = decoder_3_out_2 ? r2_q : 32'bz;  // Driver driver_11
  assign SRC2 = decoder_3_out_3 ? r3_q : 32'bz;  // Driver driver_12
  assign SRC2 = decoder_3_out_4 ? r4_q : 32'bz;  // Driver driver_13
  assign SRC2 = decoder_3_out_5 ? r5_q : 32'bz;  // Driver driver_14
  assign SRC2 = decoder_3_out_6 ? r6_q : 32'bz;  // Driver driver_15
  assign SRC2 = decoder_3_out_7 ? r7_q : 32'bz;  // Driver driver_16
endmodule
