// Digital circuit barrel_shifter_8bits.dig as structural Verilog
module barrel_shifter_8bits (
  input  EO,
  input  E1,
  input  E2,
  input  E3,
  input  E4,
  input  E5,
  input  E6,
  input  E7,
  input  I0,
  input  I1,
  input  A0,
  input  I2,
  input  A1,
  input  A2,
  input  in_23,
  input  in_24,
  input  in_25,
  input  in_26,
  output S0,
  output S1,
  output S2,
  output S3,
  output S4,
  output S5,
  output S6,
  output S7
);

  wire multiplexer_1_out, multiplexer_2_out, multiplexer_3_out, multiplexer_4_out, multiplexer_5_out,
       multiplexer_6_out, multiplexer_7_out, multiplexer_8_out, multiplexer_9_out, multiplexer_10_out,
       multiplexer_11_out, multiplexer_12_out, multiplexer_13_out, multiplexer_14_out, multiplexer_15_out,
       multiplexer_16_out;

  Multiplexer multiplexer_1 (.sel(A0), .in_0(EO), .in_1(E1), .out(multiplexer_1_out));
  Multiplexer multiplexer_2 (.in_0(E1), .in_1(E2), .out(multiplexer_2_out));  // open: sel
  Multiplexer multiplexer_3 (.in_0(E2), .in_1(E3), .out(multiplexer_3_out));  // open: sel
  Multiplexer multiplexer_4 (.in_0(E3), .in_1(E4), .out(multiplexer_4_out));  // open: sel
  Multiplexer multiplexer_5 (.in_0(E4), .in_1(E5), .out(multiplexer_5_out));  // open: sel
  Multiplexer multiplexer_6 (.in_0(E5), .in_1(E6), .out(multiplexer_6_out));  // open: sel
  Multiplexer multiplexer_7 (.in_0(E6), .in_1(E7), .out(multiplexer_7_out));  // open: sel
  Multiplexer multiplexer_8 (.in_0(E7), .in_1(I0), .out(multiplexer_8_out));  // open: sel
  Multiplexer multiplexer_9 (.sel(A1), .in_0(multiplexer_1_out), .in_1(multiplexer_2_out), .out(multiplexer_9_out));
  Multiplexer multiplexer_10 (
    .in_0(multiplexer_2_out), .in_1(multiplexer_3_out), .out(multiplexer_10_out));  // open: sel
  Multiplexer multiplexer_11 (
    .in_0(multiplexer_3_out), .in_1(multiplexer_4_out), .out(multiplexer_11_out));  // open: sel
  Multiplexer multiplexer_12 (
    .in_0(multiplexer_4_out), .in_1(multiplexer_5_out), .out(multiplexer_12_out));  // open: sel
  Multiplexer multiplexer_13 (
    .in_0(multiplexer_5_out), .in_1(multiplexer_6_out), .out(multiplexer_13_out));  // open: sel
  Multiplexer multiplexer_14 (
    .in_0(multiplexer_6_out), .in_1(multiplexer_7_out), .out(multiplexer_14_out));  // open: sel
  Multiplexer multiplexer_15 (.in_0(multiplexer_7_out), .in_1(in_23), .out(multiplexer_15_out));  // open: sel
  Multiplexer multiplexer_16 (.in_0(multiplexer_8_out), .in_1(I1), .out(multiplexer_16_out));  // open: sel
  Multiplexer multiplexer_17 (.sel(A2), .in_0(multiplexer_9_out), .in_1(multiplexer_14_out), .out(S0));
  Multiplexer multiplexer_18 (.in_0(multiplexer_10_out), .in_1(multiplexer_14_out), .out(S1));  // open: sel
  Multiplexer multiplexer_19 (.in_0(multiplexer_11_out), .in_1(multiplexer_15_out), .out(S2));  // open: sel
  Multiplexer multiplexer_20 (.in_0(multiplexer_12_out), .in_1(multiplexer_16_out), .out(S3));  // open: sel
  Multiplexer multiplexer_21 (.in_0(multiplexer_13_out), .in_1(in_26), .out(S4));  // open: sel
  Multiplexer multiplexer_22 (.in_0(multiplexer_14_out), .in_1(in_25), .out(S5));  // open: sel
  Multiplexer multiplexer_23 (.in_0(multiplexer_15_out), .in_1(in_24), .out(S6));  // open: sel
  Multiplexer multiplexer_24 (.in_0(multiplexer_16_out), .in_1(I2), .out(S7));  // open: sel
endmodule
