// Digital circuit datapath1.2.dig as structural Verilog
module datapath1_2 (
  input  W_PC,
  input  W_RI,
  input  W_MAR,
  input  W_MDR,
  input  G_PC,
  input  WRITE_MEM,
  input  G_MDR,
  input  W_reg,
  input  MUX_ALU,
  input  MUX_PC,
  input  MUX_MDR,
  input  G_ALU
);

  wire [31:0] add_1_s, banc_de_32_registres_1_src1, banc_de_32_registres_1_src2, bitextender_1_out,
       driver_1_out, MAR_q, MDR_q, multiplexer_1_out, multiplexer_2_out, PC_q, ramsingleportsel_1_d, RI_q,
       ual_1_s;

  D_FF #(.Bits(32)) RI (.D(driver_1_out), .C(W_RI), .Q(RI_q));  // open: nQ
  D_FF #(.Bits(32)) PC (.D(add_1_s), .C(W_PC), .Q(PC_q));  // open: nQ
  Add #(.Bits(32)) add_1 (.a(PC_q), .b(32'h4), .c_i(1'b0), .s(add_1_s));  // open: c_o
  assign driver_1_out = G_PC ? PC_q : 32'bz;  // Driver driver_1
  D_FF #(.Bits(32)) MAR (.D(driver_1_out), .C(W_MAR), .Q(MAR_q));  // open: nQ
  banc_de_32_registres banc_de_32_registres_1 (
    .RES(driver_1_out), .RD(RI_q[11:7]), .RS1(RI_q[19:15]), .RS2(RI_q[24:20]), .Wreg(W_reg),
    .SRC1(banc_de_32_registres_1_src1), .SRC2(banc_de_32_registres_1_src2));
  assign driver_1_out = G_MDR ? MDR_q : 32'bz;  // Driver driver_2
  BitExtender #(.inputBits(12), .outputBits(32)) bitextender_1 (.in(RI_q[31:20]), .out(bitextender_1_out));
  Multiplexer #(.Bits(32)) multiplexer_1 (
    .sel(MUX_MDR), .in_0(ramsingleportsel_1_d), .in_1(driver_1_out), .out(multiplexer_1_out));
  D_FF #(.Bits(32)) MDR (.D(multiplexer_1_out), .C(W_MDR), .Q(MDR_q));  // open: nQ
  RAMSinglePortSel #(.AddrBits(6), .Bits(32)) ramsingleportsel_1 (
    .A(MAR_q[7:2]), .CS(1'b1), .WE(WRITE_MEM), .OE(~WRITE_MEM), .D(ramsingleportsel_1_d));
  Multiplexer #(.Bits(32)) multiplexer_2 (
    .sel(MUX_ALU), .in_0(banc_de_32_registres_1_src2), .in_1(bitextender_1_out), .out(multiplexer_2_out));
  assign ramsingleportsel_1_d = WRITE_MEM ? MDR_q : 32'bz;  // Driver driver_3
  UAL ual_1 (.A(banc_de_32_registres_1_src1), .B(multiplexer_2_out), .SUB(RI_q[30]), .F3(RI_q[14:12]), .S(ual_1_s));
  assign driver_1_out = G_ALU ? ual_1_s : 32'bz;  // Driver driver_4
endmodule
