// Digital circuit MUX8en_nonrec.dig as structural Verilog
module MUX8en_nonrec (
  input  I0,
  input  I1,
  input  C0,
  input  I2,
  input  I3,
  input  A,
  input  I4,
  input  I5,
  input  A_2,
  input  I6,
  input  I7,
  input  A_3,
  input  C1,
  input  C2,
  output S
);

  wire and_1_out, and_2_out, and_3_out, and_4_out, and_5_out, and_6_out, and_7_out, and_8_out, and_9_out,
       and_10_out, and_11_out, and_12_out, and_13_out, and_14_out, not_1_out, not_2_out, not_3_out, or_1_out,
       or_2_out, or_3_out, or_4_out, or_5_out, or_6_out;

  not not_1 (not_1_out, C0);
  and and_1 (and_1_out, I0, not_1_out);
  and and_2 (and_2_out, C0, I1);
  and and_3 (and_3_out, I2, not_1_out);
  and and_4 (and_4_out, C0, I3);
  and and_5 (and_5_out, I4, not_1_out);
  and and_6 (and_6_out, C0, I5);
  and and_7 (and_7_out, I6, not_1_out);
  and and_8 (and_8_out, C0, I7);
  or or_1 (or_1_out, and_1_out, and_2_out);
  or or_2 (or_2_out, and_3_out, and_4_out);
  or or_3 (or_3_out, and_5_out, and_6_out);
  or or_4 (or_4_out, and_7_out, and_8_out);
  not not_2 (not_2_out, C1);
  and and_9 (and_9_out, or_1_out, not_2_out);
  and and_10 (and_10_out, C1, or_2_out);
  and and_11 (and_11_out, or_3_out, not_2_out);
  and and_12 (and_12_out, C1, or_4_out);
  or or_5 (or_5_out, and_9_out, and_10_out);
  or or_6 (or_6_out, and_11_out, and_12_out);
  not not_3 (not_3_out, C2);
  and and_13 (and_13_out, or_5_out, not_3_out);
  and and_14 (and_14_out, or_6_out, C2);
  or or_7 (S, and_13_out, and_14_out);
endmodule
