// Digital circuit MUX_16bits.dig as structural Verilog
module MUX_16bits (
  input  a0,
  input  b0,
  input  a1,
  input  b1,
  input  a2,
  input  b2,
  input  a3,
  input  b3,
  input  C0,
  input  C1,
  input  C2,
  input  a4,
  input  b4,
  input  a5,
  input  b5,
  input  a6,
  input  b6,
  input  a7,
  input  b7,
  input  C3,
  output S
);

  wire mux2vers1_1_s, mux2vers1_2_s, mux2vers1_3_s, mux2vers1_4_s, mux2vers1_5_s, mux2vers1_6_s,
       mux2vers1_7_s, mux2vers1_8_s, mux2vers1_9_s, mux2vers1_10_s, mux2vers1_11_s, mux2vers1_12_s,
       mux2vers1_13_s, mux2vers1_14_s;

  MUX2vers1 mux2vers1_1 (.a(a0), .b(b0), .c(C0), .S(mux2vers1_1_s));
  MUX2vers1 mux2vers1_2 (.a(a1), .b(b1), .c(C0), .S(mux2vers1_2_s));
  MUX2vers1 mux2vers1_3 (.a(a2), .b(b2), .c(C0), .S(mux2vers1_3_s));
  MUX2vers1 mux2vers1_4 (.a(a3), .b(b3), .c(C0), .S(mux2vers1_4_s));
  MUX2vers1 mux2vers1_5 (.a(a4), .b(b4), .c(C0), .S(mux2vers1_5_s));
  MUX2vers1 mux2vers1_6 (.a(a5), .b(b5), .c(C0), .S(mux2vers1_6_s));
  MUX2vers1 mux2vers1_7 (.a(a6), .b(b6), .c(C0), .S(mux2vers1_7_s));
  MUX2vers1 mux2vers1_8 (.a(a7), .b(b7), .c(C0), .S(mux2vers1_8_s));
  MUX2vers1 mux2vers1_9 (.a(mux2vers1_1_s), .b(mux2vers1_2_s), .c(C1), .S(mux2vers1_9_s));
  MUX2vers1 mux2vers1_10 (.a(mux2vers1_3_s), .b(mux2vers1_4_s), .c(C1), .S(mux2vers1_10_s));
  MUX2vers1 mux2vers1_11 (.a(mux2vers1_5_s), .b(mux2vers1_6_s), .c(C1), .S(mux2vers1_11_s));
  MUX2vers1 mux2vers1_12 (.a(mux2vers1_7_s), .b(mux2vers1_8_s), .c(C1), .S(mux2vers1_12_s));
  MUX2vers1 mux2vers1_13 (.a(mux2vers1_9_s), .b(mux2vers1_10_s), .c(C2), .S(mux2vers1_13_s));
  MUX2vers1 mux2vers1_14 (.a(mux2vers1_11_s), .b(mux2vers1_12_s), .c(C2), .S(mux2vers1_14_s));
  MUX2vers1 mux2vers1_15 (.a(mux2vers1_13_s), .b(mux2vers1_14_s), .c(C3), .S(S));
endmodule
