// Digital circuit MUX_8en_rec.dig as structural Verilog
module MUX_8en_rec (
  input  e0,
  input  e1,
  input  e2,
  input  e3,
  input  e4,
  input  e5,
  input  e6,
  input  e7,
  input  C0,
  input  C1,
  input  C2,
  output S
);

  wire mux2vers1_1_s, mux2vers1_2_s, mux2vers1_3_s, mux2vers1_4_s, mux2vers1_5_s, mux2vers1_6_s;

  MUX2vers1 mux2vers1_1 (.a(e0), .b(e1), .c(C0), .S(mux2vers1_1_s));
  MUX2vers1 mux2vers1_2 (.a(e2), .b(e3), .c(C0), .S(mux2vers1_2_s));
  MUX2vers1 mux2vers1_3 (.a(e4), .b(e5), .c(C0), .S(mux2vers1_3_s));
  MUX2vers1 mux2vers1_4 (.a(e6), .b(e7), .c(C0), .S(mux2vers1_4_s));
  MUX2vers1 mux2vers1_5 (.a(mux2vers1_1_s), .b(mux2vers1_2_s), .c(C1), .S(mux2vers1_5_s));
  MUX2vers1 mux2vers1_6 (.a(mux2vers1_3_s), .b(mux2vers1_4_s), .c(C1), .S(mux2vers1_6_s));
  MUX2vers1 mux2vers1_7 (.a(mux2vers1_5_s), .b(mux2vers1_6_s), .c(C2), .S(S));
endmodule
