// Digital circuit Circuit_controle.dig as structural Verilog
module Circuit_controle (
  input  fin,
  input  clk,
  output E0,
  output E1
);

  wire and_1_out, not_1_out, or_1_out;

  and and_1 (and_1_out, fin, E0);
  or or_1 (or_1_out, E1, and_1_out);
  not not_1 (not_1_out, or_1_out);
  D_FF d_ff_1 (.D(or_1_out), .C(clk), .Q(E1));  // open: nQ
  D_FF d_ff_2 (.D(not_1_out), .C(clk), .Q(E0));  // open: nQ
endmodule
