// Digital circuit compt_1bit.dig as structural Verilog
module compt_1bit (
  input  clk,
  output Q0,
  output Q1
);

  wire not_1_out, xor_1_out;

  xor xor_1 (xor_1_out, Q0, Q1);
  not not_1 (not_1_out, Q0);
  D_FF d_ff_1 (.D(not_1_out), .C(clk), .Q(Q0));  // open: nQ
  D_FF d_ff_2 (.D(xor_1_out), .C(clk), .Q(Q1));  // open: nQ
endmodule
