// Digital circuit reg_dec_4bits.dig as structural Verilog
module reg_dec_4bits (
  input  [3:0] a,
  input  dec,
  input  clk,
  output [3:0] S
);

  wire mux2vers1_1_s, mux2vers1_2_s, mux2vers1_3_s, mux2vers1_4_s;

  MUX2vers1 mux2vers1_1 (.a(a[0]), .b(S[1]), .c(dec), .S(mux2vers1_1_s));
  MUX2vers1 mux2vers1_2 (.a(a[1]), .b(S[2]), .c(dec), .S(mux2vers1_2_s));
  MUX2vers1 mux2vers1_3 (.a(a[2]), .b(S[3]), .c(dec), .S(mux2vers1_3_s));
  MUX2vers1 mux2vers1_4 (.a(a[3]), .b(1'b0), .c(dec), .S(mux2vers1_4_s));
  D_FF d_ff_1 (.D(mux2vers1_1_s), .C(clk), .Q(S[0]));  // open: nQ
  D_FF d_ff_2 (.D(mux2vers1_2_s), .C(clk), .Q(S[1]));  // open: nQ
  D_FF d_ff_3 (.D(mux2vers1_3_s), .C(clk), .Q(S[2]));  // open: nQ
  D_FF d_ff_4 (.D(mux2vers1_4_s), .C(clk), .Q(S[3]));  // open: nQ
endmodule
