// Digital circuit Registre-simple.dig as structural Verilog
module Registre_simple (
  input  Clk,
  input  [7:0] a,
  output [7:0] S
);

  D_FF d_ff_1 (.D(a[7]), .C(Clk), .Q(S[7]));  // open: nQ
  D_FF d_ff_2 (.D(a[6]), .C(Clk), .Q(S[6]));  // open: nQ
  D_FF d_ff_3 (.D(a[5]), .C(Clk), .Q(S[5]));  // open: nQ
  D_FF d_ff_4 (.D(a[4]), .C(Clk), .Q(S[4]));  // open: nQ
  D_FF d_ff_5 (.D(a[3]), .C(Clk), .Q(S[3]));  // open: nQ
  D_FF d_ff_6 (.D(a[2]), .C(Clk), .Q(S[2]));  // open: nQ
  D_FF d_ff_7 (.D(a[1]), .C(Clk), .Q(S[1]));  // open: nQ
  D_FF d_ff_8 (.D(a[0]), .C(Clk), .Q(S[0]));  // open: nQ
endmodule
