// Digital circuit Registre_dec_g&d.dig as structural Verilog
module Registre_dec_g_d (
  input  left,
  input  [7:0] a,
  input  clk,
  input  Dec,
  output [7:0] S
);

  wire [7:0] mux2vers1_1_s, regidtre_dec_droite_1_s, registe_dec_gauche_1_s;

  Regidtre_dec_droite regidtre_dec_droite_1 (.Clk(clk), .a(a), .Dec(Dec), .S(regidtre_dec_droite_1_s));
  Registe_dec_gauche registe_dec_gauche_1 (.Clk(clk), .a(a), .Dec(Dec), .S(registe_dec_gauche_1_s));
  MUX2vers1 mux2vers1_1 (.a(regidtre_dec_droite_1_s[0]), .b(registe_dec_gauche_1_s[0]), .c(left), .S(mux2vers1_1_s[0]));
  MUX2vers1 mux2vers1_2 (.a(regidtre_dec_droite_1_s[1]), .b(registe_dec_gauche_1_s[1]), .c(left), .S(mux2vers1_1_s[1]));
  MUX2vers1 mux2vers1_3 (.a(regidtre_dec_droite_1_s[2]), .b(registe_dec_gauche_1_s[2]), .c(left), .S(mux2vers1_1_s[2]));
  MUX2vers1 mux2vers1_4 (.a(regidtre_dec_droite_1_s[3]), .b(registe_dec_gauche_1_s[3]), .c(left), .S(mux2vers1_1_s[3]));
  MUX2vers1 mux2vers1_5 (.a(regidtre_dec_droite_1_s[4]), .b(registe_dec_gauche_1_s[4]), .c(left), .S(mux2vers1_1_s[4]));
  MUX2vers1 mux2vers1_6 (.a(regidtre_dec_droite_1_s[5]), .b(registe_dec_gauche_1_s[5]), .c(left), .S(mux2vers1_1_s[5]));
  MUX2vers1 mux2vers1_7 (.a(regidtre_dec_droite_1_s[6]), .b(registe_dec_gauche_1_s[6]), .c(left), .S(mux2vers1_1_s[6]));
  MUX2vers1 mux2vers1_8 (.a(regidtre_dec_droite_1_s[7]), .b(registe_dec_gauche_1_s[7]), .c(left), .S(mux2vers1_1_s[7]));
  Registre_simple registre_simple_1 (.Clk(clk), .a(mux2vers1_1_s), .S(S));
endmodule
