// Digital circuit Regidtre_dec_droite.dig as structural Verilog
module Regidtre_dec_droite (
  input  Clk,
  input  [7:0] a,
  input  Dec,
  output [7:0] S
);

  wire mux2vers1_1_s, mux2vers1_2_s, mux2vers1_3_s, mux2vers1_4_s, mux2vers1_5_s, mux2vers1_6_s,
       mux2vers1_7_s, mux2vers1_8_s;

  MUX2vers1 mux2vers1_1 (.a(a[0]), .b(a[1]), .c(Dec), .S(mux2vers1_1_s));
  MUX2vers1 mux2vers1_2 (.a(a[1]), .b(a[2]), .c(Dec), .S(mux2vers1_2_s));
  MUX2vers1 mux2vers1_3 (.a(a[2]), .b(a[3]), .c(Dec), .S(mux2vers1_3_s));
  MUX2vers1 mux2vers1_4 (.a(a[3]), .b(a[4]), .c(Dec), .S(mux2vers1_4_s));
  MUX2vers1 mux2vers1_5 (.a(a[4]), .b(a[5]), .c(Dec), .S(mux2vers1_5_s));
  MUX2vers1 mux2vers1_6 (.a(a[5]), .b(a[6]), .c(Dec), .S(mux2vers1_6_s));
  MUX2vers1 mux2vers1_7 (.a(a[6]), .b(a[7]), .c(Dec), .S(mux2vers1_7_s));
  MUX2vers1 mux2vers1_8 (.a(a[7]), .b(1'b0), .c(Dec), .S(mux2vers1_8_s));
  D_FF d_ff_1 (.D(mux2vers1_1_s), .C(Clk), .Q(S[0]));  // open: nQ
  D_FF d_ff_2 (.D(mux2vers1_2_s), .C(Clk), .Q(S[1]));  // open: nQ
  D_FF d_ff_3 (.D(mux2vers1_3_s), .C(Clk), .Q(S[2]));  // open: nQ
  D_FF d_ff_4 (.D(mux2vers1_4_s), .C(Clk), .Q(S[3]));  // open: nQ
  D_FF d_ff_5 (.D(mux2vers1_5_s), .C(Clk), .Q(S[4]));  // open: nQ
  D_FF d_ff_6 (.D(mux2vers1_6_s), .C(Clk), .Q(S[5]));  // open: nQ
  D_FF d_ff_7 (.D(mux2vers1_7_s), .C(Clk), .Q(S[6]));  // open: nQ
  D_FF d_ff_8 (.D(mux2vers1_8_s), .C(Clk), .Q(S[7]));  // open: nQ
endmodule
