// Digital circuit SUB.dig as structural Verilog
module SUB (
  input  SUB,
  input  [7:0] b,
  input  [7:0] a,
  output Cout,
  output [7:0] S
);

  wire add1bit_1_cout, add1bit_2_cout, add1bit_3_cout, add1bit_4_cout, add1bit_5_cout, add1bit_6_cout,
       add1bit_7_cout, xor_1_out, xor_2_out, xor_3_out, xor_4_out, xor_5_out, xor_6_out, xor_7_out, xor_8_out;

  xor xor_1 (xor_1_out, b[0], SUB);
  xor xor_2 (xor_2_out, b[1], SUB);
  ADD1bit add1bit_1 (.a(a[0]), .b(xor_1_out), .Cin(SUB), .S(S[0]), .Cout(add1bit_1_cout));
  xor xor_3 (xor_3_out, b[2], SUB);
  ADD1bit add1bit_2 (.a(a[1]), .b(xor_2_out), .Cin(add1bit_1_cout), .S(S[1]), .Cout(add1bit_2_cout));
  xor xor_4 (xor_4_out, b[3], SUB);
  ADD1bit add1bit_3 (.a(a[2]), .b(xor_3_out), .Cin(add1bit_2_cout), .S(S[2]), .Cout(add1bit_3_cout));
  xor xor_5 (xor_5_out, b[4], SUB);
  ADD1bit add1bit_4 (.a(a[3]), .b(xor_4_out), .Cin(add1bit_3_cout), .S(S[3]), .Cout(add1bit_4_cout));
  ADD1bit add1bit_5 (.a(a[4]), .b(xor_5_out), .Cin(add1bit_4_cout), .S(S[4]), .Cout(add1bit_5_cout));
  xor xor_6 (xor_6_out, b[5], SUB);
  xor xor_7 (xor_7_out, b[6], SUB);
  ADD1bit add1bit_6 (.a(a[5]), .b(xor_6_out), .Cin(add1bit_5_cout), .S(S[5]), .Cout(add1bit_6_cout));
  xor xor_8 (xor_8_out, b[7], SUB);
  ADD1bit add1bit_7 (.a(a[6]), .b(xor_7_out), .Cin(add1bit_6_cout), .S(S[6]), .Cout(add1bit_7_cout));
  ADD1bit add1bit_8 (.a(a[7]), .b(xor_8_out), .Cin(add1bit_7_cout), .S(S[7]), .Cout(Cout));
endmodule
