// Digital circuit UAL_32b.dig as structural Verilog
module UAL_32b (
  input  [31:0] a,
  input  [31:0] b,
  input  SUB,
  input  [2:0] f3,
  output [31:0] S
);

  wire [31:0] add_1_s, and_1_out, multiplexer_1_out, or_1_out, sub_1_s, xor_1_out;

  Add #(.Bits(32)) add_1 (.a(a), .b(b), .c_i(1'b0), .s(add_1_s));  // open: c_o
  Sub #(.Bits(32)) sub_1 (.a(a), .b(b), .c_i(1'b0), .s(sub_1_s));  // open: c_o
  assign xor_1_out = a ^ b;  // XOr xor_1, 32 bits wide
  assign and_1_out = a & b;  // And and_1, 32 bits wide
  assign or_1_out = a | b;  // Or or_1, 32 bits wide
  Multiplexer #(.Bits(32)) multiplexer_1 (.sel(SUB), .in_0(add_1_s), .in_1(sub_1_s), .out(multiplexer_1_out));
  Multiplexer #(.Selector_Bits(3), .Bits(32)) multiplexer_2 (
    .sel(f3), .in_0(multiplexer_1_out), .in_1(xor_1_out), .in_2(and_1_out), .in_3(or_1_out),
    .in_4({32{1'b0}}), .in_5({32{1'b0}}), .in_6({32{1'b0}}), .in_7({32{1'b0}}), .out(S));
endmodule
