// Digital circuit multiplieur_seqquentiel.dig as structural Verilog
module multiplieur_seqquentiel (
  input  [3:0] OP1,
  input  Clk,
  input  [3:0] OP2,
  output [7:0] RES
);

  wire and_1_out, circuit_controle_1_e0, circuit_controle_1_e1, compt_1bit_1_q0, compt_1bit_1_q1, or_1_out;
  wire [3:0] reg_dec_4bits_1_s;
  wire [7:0] add8bit_1_p18, bitextender_1_out, multiplexer_1_out, multiplexer_2_out, registe_dec_gauche_1_s;

  BitExtender #(.inputBits(4), .outputBits(8)) bitextender_1 (.in(OP1), .out(bitextender_1_out));
  compt_1bit compt_1bit_1 (.clk(Clk), .Q0(compt_1bit_1_q0), .Q1(compt_1bit_1_q1));
  and and_1 (and_1_out, compt_1bit_1_q0, compt_1bit_1_q1);
  Registe_dec_gauche registe_dec_gauche_1 (
    .Clk(Clk), .a(bitextender_1_out), .Dec(circuit_controle_1_e0), .S(registe_dec_gauche_1_s));
  reg_dec_4bits reg_dec_4bits_1 (.a(OP2), .dec(circuit_controle_1_e0), .clk(Clk), .S(reg_dec_4bits_1_s));
  Circuit_controle circuit_controle_1 (
    .fin(and_1_out), .clk(Clk), .E0(circuit_controle_1_e0), .E1(circuit_controle_1_e1));
  Multiplexer #(.Bits(8)) multiplexer_1 (
    .sel(reg_dec_4bits_1_s[0]), .in_0({8{1'b0}}), .in_1(registe_dec_gauche_1_s), .out(multiplexer_1_out));
  or or_1 (or_1_out, circuit_controle_1_e0, circuit_controle_1_e1);
  // Add8bit add8bit_1: pin names not known; wires that end beside it: multiplexer_1_out[0], RES[0], multiplexer_1_out[1], RES[4], multiplexer_1_out[2], RES[1], RES[2], multiplexer_1_out[4], multiplexer_1_out[3], RES[3], multiplexer_1_out[5], RES[5], multiplexer_1_out[7], multiplexer_1_out[6], 1'b0, RES[7], RES[6], add8bit_1_p18[0], add8bit_1_p18[1], add8bit_1_p18[2], add8bit_1_p18[5], add8bit_1_p18[6], add8bit_1_p18[3], add8bit_1_p18[4], add8bit_1_p18[7]
  Multiplexer #(.Bits(8)) multiplexer_2 (
    .sel(or_1_out), .in_0({8{1'b0}}), .in_1(add8bit_1_p18), .out(multiplexer_2_out));
  Registre_simple registre_simple_1 (.Clk(Clk), .a(multiplexer_2_out), .S(RES));
endmodule
